// Logisim project bcd.circ as structural Verilog: 1 circuit, main circuit implementation
module implementation (
  input  w3,
  input  w2,
  input  w1,
  input  w0,
  output a,
  output b,
  output c,
  output d,
  output e,
  output f,
  output g
);

  wire and_1_out, and_2_out, and_3_out, and_4_out, and_5_out, and_6_out, and_7_out, and_8_out, and_9_out,
       and_10_out, and_11_out, and_12_out, and_13_out, and_14_out, and_15_out, and_16_out, and_17_out,
       and_18_out, and_19_out, not_1_out, not_2_out, not_3_out, not_4_out, not_5_out, not_6_out, not_7_out,
       not_8_out, not_9_out, not_10_out, not_11_out, not_12_out, not_13_out, not_14_out, not_15_out,
       not_16_out, not_17_out, not_18_out, not_19_out, not_20_out, not_21_out, not_22_out, not_23_out;

  and and_1 (and_1_out, w0, w2);
  not not_1 (not_1_out, w0);
  and and_2 (and_2_out, not_1_out, not_2_out);
  not not_2 (not_2_out, w2);
  not not_3 (not_3_out, w2);
  not not_4 (not_4_out, w0);
  and and_3 (and_3_out, not_4_out, not_5_out);
  not not_5 (not_5_out, w1);
  and and_4 (and_4_out, w0, w1);
  not not_6 (not_6_out, w0);
  and and_5 (and_5_out, not_6_out, not_7_out);
  not not_7 (not_7_out, w2);
  and and_6 (and_6_out, w1, not_8_out);
  not not_8 (not_8_out, w2);
  not not_9 (not_9_out, w0);
  and and_7 (and_7_out, not_9_out, w1);
  not not_10 (not_10_out, w1);
  or or_1 (a, w3, w1, and_1_out, and_2_out);
  or or_2 (b, not_3_out, and_3_out, and_4_out);
  or or_3 (d, and_5_out, and_6_out, and_7_out, w3, and_8_out);
  and and_8 (and_8_out, not_10_out, w2, w0);
  not not_11 (not_11_out, w2);
  not not_12 (not_12_out, w0);
  not not_13 (not_13_out, w1);
  and and_9 (and_9_out, w1, not_11_out);
  and and_10 (and_10_out, not_12_out, w2);
  and and_11 (and_11_out, not_13_out, w2);
  not not_14 (not_14_out, w1);
  and and_12 (and_12_out, not_14_out, not_15_out);
  not not_15 (not_15_out, w0);
  and and_13 (and_13_out, w1, w0);
  not not_16 (not_16_out, w1);
  and and_14 (and_14_out, not_16_out, w0);
  not not_17 (not_17_out, w0);
  and and_15 (and_15_out, not_17_out, not_18_out);
  not not_18 (not_18_out, w2);
  not not_19 (not_19_out, w0);
  and and_16 (and_16_out, not_19_out, w1);
  not not_20 (not_20_out, w0);
  and and_17 (and_17_out, not_20_out, not_21_out);
  not not_21 (not_21_out, w1);
  not not_22 (not_22_out, w0);
  and and_18 (and_18_out, not_22_out, w2);
  not not_23 (not_23_out, w1);
  and and_19 (and_19_out, not_23_out, w2);
  or or_4 (g, and_9_out, w3, and_10_out, and_11_out);
  or or_5 (c, and_12_out, and_13_out, and_14_out, w2);
  or or_6 (e, and_15_out, and_16_out);
  or or_7 (f, and_17_out, w3, and_18_out, and_19_out);

  // Other names for the same wires on the sheet: at = a; bt = b; ct = c; dt = d; et = e; ft = f; gt = g; w0t = w0;
  //   w1t = w1; w2t = w2; w3t = w3
endmodule
