// Logisim project fun.circ as structural Verilog: 1 circuit, main circuit implementation
module implementation (
  input  x3,
  input  x2,
  input  x1,
  input  x0,
  output the_output
);

  wire p1, p2;

  and and_1 (p1, x2, x3);
  and and_2 (p2, x0, x1);
  or or_1 (the_output, p1, p2);

  // Other names for the same wires on the sheet: the_output_t = the_output; x0t = x0; x1t = x1; x2t = x2; x3t = x3
endmodule
