// Logisim project Cache.circ as structural Verilog: 5 circuits, main circuit set
module implementation (
  input  [9:0] CpuAddressIn,
  input  CpuReadIn,
  input  CpuWriteIn,
  input  [7:0] CpuWriteValueIn,
  input  [31:0] LineFromMemIn,
  input  ClkIn,
  output ReadyOut,
  output DidContainOut,
  output [7:0] ByteReadOut,
  output [7:0] MemAddressOut,
  output MemReadOut,
  output MemWriteOut,
  output [31:0] Line2MemOut
);

  wire age1, age2, and_1_out, cahngeAge, cahngeAge1, cahngeAge2, changed_dirty1, changed_dirty2, contains,
       contains1, contains2, dirtyTag, initiall, one, read, three, two, write, write1, write2, write_start,
       write_val;
  wire [1:0] offset1, offset2;
  wire [2:0] fsm_1_threee;
  wire [6:0] changed_tag1, changed_tag2, multiplexer_1_out, tag1, tag2;
  wire [7:0] byteread1, byteread2, CPU_val1, CPU_val2, writeVal;
  wire [9:0] CpuAdress;
  wire [31:0] cahngedLine1, cahngedLine2, line1, line2;

  Register #(.width(10)) register_1 (.D(CpuAddressIn), .en(ReadyOut), .clk(ClkIn), .Q(CpuAdress));  // open: clr
  Register #(.width(1)) register_2 (.D(CpuReadIn), .en(ReadyOut), .clk(ClkIn), .Q(read));  // open: clr
  Register #(.width(1)) register_3 (.D(CpuWriteIn), .en(ReadyOut), .clk(ClkIn), .Q(write));  // open: clr
  Register register_4 (.D(CpuWriteValueIn), .en(ReadyOut), .clk(ClkIn), .Q(writeVal));  // open: clr
  Multiplexer #(.enable("false"), .width(7)) multiplexer_1 (
    .in0(changed_tag1), .in1(changed_tag2), .out(multiplexer_1_out), .sel(CpuAdress[2]));
  Multiplexer #(.enable("false")) multiplexer_2 (.in0(contains1), .in1(contains2), .out(contains), .sel(CpuAdress[2]));
  FSM fsm_1 (
    .three(three), .two(two), .one(one), .Read(read), .Write(write), .Contains(contains),
    .olddirty(dirtyTag), .third(three), .second(two), .first(one), .readd(read), .writee(write),
    .contain(DidContainOut), .old(dirtyTag), .threee(fsm_1_threee[0]), .twoo(fsm_1_threee[1]),
    .onee(fsm_1_threee[2]), .intial(initiall), .ready(ReadyOut), .readmem(MemReadOut),
    .writemen(MemWriteOut), .writeStart(write_start), .write_val(write_val), .changeAge(cahngeAge));
  Multiplexer #(.enable("false"), .select(2), .width(8)) multiplexer_3 (
    .in1({multiplexer_1_out, CpuAdress[2]}), .in2(CpuAddressIn[9:2]), .out(MemAddressOut),
    .sel({MemReadOut, MemWriteOut}));  // open: in0, in3
  Demultiplexer #(.enable("false"), .width(7)) demultiplexer_1 (
    .out0(tag1), .out1(tag2), .in(CpuAdress[9:3]), .sel(CpuAdress[2]));
  Demultiplexer #(.enable("false"), .width(32)) demultiplexer_2 (
    .out0(line1), .out1(line2), .in(LineFromMemIn), .sel(CpuAdress[2]));
  Demultiplexer #(.enable("false")) demultiplexer_3 (
    .out0(write1), .out1(write2), .in(write_start), .sel(CpuAdress[2]));
  Multiplexer #(.enable("false")) multiplexer_4 (.in0(age1), .in1(1'b1), .out(cahngeAge1), .sel(initiall));
  Multiplexer #(.enable("false")) multiplexer_5 (
    .in0(changed_dirty1), .in1(changed_dirty2), .out(dirtyTag), .sel(CpuAdress[2]));
  Register #(.width(3)) register_5 (.D(fsm_1_threee), .clk(ClkIn), .Q({one, two, three}));  // open: en, clr
  Demultiplexer #(.enable("false"), .width(2)) demultiplexer_4 (
    .out0(offset1), .out1(offset2), .in(CpuAdress[1:0]), .sel(CpuAdress[2]));
  Multiplexer #(.enable("false")) multiplexer_6 (.in0(age2), .in1(1'b1), .out(cahngeAge2), .sel(initiall));
  Demultiplexer #(.enable("false"), .width(8)) demultiplexer_5 (
    .out0(CPU_val1), .out1(CPU_val2), .in(writeVal), .sel(CpuAdress[2]));
  Demultiplexer #(.enable("false")) demultiplexer_6 (.out0(age1), .out1(age2), .in(cahngeAge), .sel(CpuAdress[2]));
  Multiplexer #(.enable("false"), .width(8)) multiplexer_7 (
    .in0(byteread1), .in1(byteread2), .out(ByteReadOut), .sel(CpuAdress[2]));
  Multiplexer #(.enable("false"), .width(32)) multiplexer_8 (
    .in0(cahngedLine1), .in1(cahngedLine2), .out(Line2MemOut), .sel(CpuAdress[2]));
  Register #(.width(1)) register_6 (.D(contains), .en(and_1_out), .clk(ClkIn), .Q(DidContainOut));  // open: clr
  and and_1 (and_1_out, ~one, two, ~three);  // AND_Gate
  set set_1 (
    .tag(tag1), .initiall(initiall), .changeAge(cahngeAge1), .offset(offset1), .LineFromMem(line1),
    .write(write1), .writeval(write_val), .cpuwrite(CPU_val1), .clk(ClkIn), .contains(contains1),
    .byteRead(byteread1), .oldTag(changed_tag1), .oldDirty(changed_dirty1), .oldLine(cahngedLine1));
  set set_2 (
    .tag(tag2), .initiall(initiall), .changeAge(cahngeAge2), .offset(offset2), .LineFromMem(line2),
    .write(write2), .writeval(write_val), .cpuwrite(CPU_val2), .clk(ClkIn), .contains(contains2),
    .byteRead(byteread2), .oldTag(changed_tag2), .oldDirty(changed_dirty2), .oldLine(cahngedLine2));
  // Probe on byteread2

  // Other names for the same wires on the sheet: MemWrite = MemWriteOut; MemRead = MemReadOut; clk = ClkIn;
  //   CpuAddress[9:0] = CpuAddressIn; offset[1:0] = CpuAdress[1:0]; sset = CpuAdress[2]; tag[6:0] = CpuAdress[9:3];
  //   CpuRead = CpuReadIn; CpuWrite = CpuWriteIn; CpuWriteValue[7:0] = CpuWriteValueIn; DidContain = DidContainOut;
  //   LineFromMem[31:0] = LineFromMemIn; MemAddress[7:0] = MemAddressOut; Ready = ReadyOut;
  //   ByteRead[7:0] = ByteReadOut; SelectedSetByteRead[7:0] = ByteReadOut; Line2Mem[31:0] = Line2MemOut;
  //   SelectedSetLine2Mem[31:0] = Line2MemOut
endmodule

module set (
  input  [6:0] tag,
  input  initiall,
  input  changeAge,
  input  [1:0] offset,
  input  [31:0] LineFromMem,
  input  write,
  input  writeval,
  input  [7:0] cpuwrite,
  input  clk,
  output contains,
  output [7:0] byteRead,
  output [6:0] oldTag,
  output oldDirty,
  output [31:0] oldLine
);

  wire and_1_out, and_2_out, and_3_out, and_4_out, and_5_out, and_6_out, and_7_out, and_8_out, and_9_out,
       and_10_out, contain1, contain2, contain3, dirty1, dirty2, dirty3, not_1_out, not_2_out, not_3_out,
       not_4_out, not_5_out, not_6_out, write1, write2, write3;
  wire [1:0] age1, age2, age3, age_new, cur_age1, cur_age2, cur_age3, multiplexer_4_out, Num_chose, old;
  wire [6:0] cur_tag1, cur_tag2, cur_tag3;
  wire [7:0] cupwriteVal1, cupwriteVal2, cupwriteVal3, cur_byte1, cur_byte2, cur_byte3;
  wire [31:0] cur_line1, cur_line2, cur_line3, LineFromMem1, LineFromMem2, LineFromMem3;

  Demultiplexer #(.enable("false"), .select(2), .width(32)) demultiplexer_1 (
    .out0(LineFromMem1), .out1(LineFromMem2), .out2(LineFromMem3), .in(LineFromMem), .sel(old));  // open: out3
  Demultiplexer #(.enable("false"), .select(2), .width(8)) demultiplexer_2 (
    .out0(cupwriteVal1), .out1(cupwriteVal2), .out2(cupwriteVal3), .in(cpuwrite), .sel(Num_chose));  // open: out3
  Multiplexer #(.enable("false"), .select(2), .width(32)) multiplexer_1 (
    .in0(cur_line1), .in1(cur_line2), .in2(cur_line3), .out(oldLine), .sel(old));  // open: in3
  Multiplexer #(.enable("false"), .select(2), .width(8)) multiplexer_2 (
    .in0(cur_byte1), .in1(cur_byte2), .in2(cur_byte3), .out(byteRead), .sel(Num_chose));  // open: in3
  not not_1 (not_1_out, cur_age1[1]);
  not not_2 (not_2_out, cur_age1[0]);
  not not_3 (not_3_out, cur_age2[1]);
  not not_4 (not_4_out, cur_age2[0]);
  not not_5 (not_5_out, cur_age3[1]);
  not not_6 (not_6_out, cur_age3[0]);
  and and_1 (and_1_out, not_1_out, not_2_out, not_3_out, cur_age3[0]);
  and and_2 (and_2_out, not_1_out, not_3_out, cur_age3[1]);
  and and_3 (and_3_out, not_1_out, not_4_out, cur_age3[1]);
  and and_4 (and_4_out, not_1_out, cur_age3[1], cur_age3[0]);
  and and_5 (and_5_out, not_2_out, cur_age3[1], cur_age3[0]);
  and and_6 (and_6_out, not_1_out, not_2_out, cur_age2[0], not_5_out, not_6_out);
  and and_7 (and_7_out, not_1_out, cur_age2[1], not_5_out);
  and and_8 (and_8_out, not_1_out, cur_age2[1], cur_age2[0], not_6_out);
  and and_9 (and_9_out, not_2_out, cur_age2[1], cur_age2[0], not_5_out);
  and and_10 (and_10_out, not_2_out, cur_age2[1], cur_age2[0], not_6_out);
  Multiplexer #(.enable("false"), .select(2), .width(2)) multiplexer_3 (
    .in0(cur_age1), .in1(cur_age2), .in2(cur_age3), .out(age_new), .sel(Num_chose));  // open: in3
  or or_1 (old[1], and_1_out, and_2_out, and_3_out, and_4_out, and_5_out);
  or or_2 (old[0], and_6_out, and_7_out, and_8_out, and_9_out, and_10_out);
  Multiplexer #(.enable("false"), .width(2)) multiplexer_4 (
    .in0(old), .in1(Num_chose), .out(multiplexer_4_out), .sel(writeval));
  Demultiplexer #(.enable("false"), .select(2)) demultiplexer_3 (
    .out0(write1), .out1(write2), .out2(write3), .in(write), .sel(multiplexer_4_out));  // open: out3
  way way_1 (
    .tag(tag), .age(age1), .age_change(changeAge), .ofset(offset), .LFM(LineFromMem1), .wriite(write1),
    .wriite_val(writeval), .clk(clk), .CPUVal(cupwriteVal1), .current_tag(cur_tag1), .current_age(cur_age1),
    .contain(contain1), .isDirty(dirty1), .byteRead(cur_byte1), .current_line(cur_line1));
  way way_2 (
    .tag(tag), .age(age2), .age_change(changeAge), .ofset(offset), .LFM(LineFromMem2), .wriite(write2),
    .wriite_val(writeval), .clk(clk), .CPUVal(cupwriteVal2), .current_tag(cur_tag2), .current_age(cur_age2),
    .contain(contain2), .isDirty(dirty2), .byteRead(cur_byte2), .current_line(cur_line2));
  way way_3 (
    .tag(tag), .age(age3), .age_change(changeAge), .ofset(offset), .LFM(LineFromMem3), .wriite(write3),
    .wriite_val(writeval), .clk(clk), .CPUVal(cupwriteVal3), .current_tag(cur_tag3), .current_age(cur_age3),
    .contain(contain3), .isDirty(dirty3), .byteRead(cur_byte3), .current_line(cur_line3));
  BitFinder #(.width(3)) bitfinder_1 (.in({contain3, contain2, contain1}), .index(Num_chose), .found(contains));
  Multiplexer #(.enable("false"), .select(2)) multiplexer_5 (
    .in0(dirty1), .in1(dirty2), .in2(dirty3), .out(oldDirty), .sel(old));  // open: in3
  Multiplexer #(.enable("false"), .select(2), .width(7)) multiplexer_6 (
    .in0(cur_tag1), .in1(cur_tag2), .in2(cur_tag3), .out(oldTag), .sel(old));  // open: in3
  age_change age_change_1 (
    .cur_age(cur_age1), .agetochagne(age_new), .beginnVal(2'b00), .beginn(initiall), .age_changed(age1));
  age_change age_change_2 (
    .cur_age(cur_age2), .agetochagne(age_new), .beginnVal(2'b01), .beginn(initiall), .age_changed(age2));
  age_change age_change_3 (
    .cur_age(cur_age3), .agetochagne(age_new), .beginnVal(2'b10), .beginn(initiall), .age_changed(age3));

  // Other names for the same wires on the sheet: cupwriteVal[7:0] = cpuwrite; oldirty = oldDirty;
  //   oldway[31:0] = oldLine; write_val = writeval
endmodule

module way (
  input  [6:0] tag,
  input  [1:0] age,
  input  age_change,
  input  [1:0] ofset,
  input  [31:0] LFM,
  input  wriite,
  input  wriite_val,
  input  clk,
  input  [7:0] CPUVal,
  output [6:0] current_tag,
  output [1:0] current_age,
  output contain,
  output isDirty,
  output [7:0] byteRead,
  output [31:0] current_line
);

  wire comparator_1_eq, cur_valid, four, one, three, two, write1, write2, write3, write4;
  wire [7:0] First, Fourth, Second, Third;

  Demultiplexer #(.enable("false"), .select(2)) demultiplexer_1 (
    .out0(one), .out1(two), .out2(three), .out3(four), .in(wriite), .sel(ofset));
  Multiplexer #(.enable("false"), .width(8)) multiplexer_1 (
    .in0(LFM[7:0]), .in1(CPUVal), .out(First), .sel(wriite_val));
  Multiplexer #(.enable("false"), .width(8)) multiplexer_2 (
    .in0(LFM[15:8]), .in1(CPUVal), .out(Second), .sel(wriite_val));
  Multiplexer #(.enable("false"), .width(8)) multiplexer_3 (
    .in0(LFM[23:16]), .in1(CPUVal), .out(Third), .sel(wriite_val));
  Multiplexer #(.enable("false"), .width(8)) multiplexer_4 (
    .in0(LFM[31:24]), .in1(CPUVal), .out(Fourth), .sel(wriite_val));
  Register #(.width(7)) register_1 (.D(tag), .en(wriite), .clk(clk), .Q(current_tag));  // open: clr
  Register #(.width(2)) register_2 (.D(age), .en(age_change), .clk(clk), .Q(current_age));  // open: clr
  Register #(.width(1)) register_3 (.D(wriite), .en(wriite), .clk(clk), .Q(cur_valid));  // open: clr
  Register #(.width(1)) register_4 (.D(wriite_val), .en(wriite), .clk(clk), .Q(isDirty));  // open: clr
  Multiplexer #(.enable("false")) multiplexer_5 (.in0(wriite), .in1(one), .out(write1), .sel(wriite_val));
  Multiplexer #(.enable("false")) multiplexer_6 (.in0(wriite), .in1(three), .out(write3), .sel(wriite_val));
  Register register_5 (.D(First), .en(write1), .clk(clk), .Q(current_line[7:0]));  // open: clr
  Register register_6 (.D(Second), .en(write2), .clk(clk), .Q(current_line[15:8]));  // open: clr
  Register register_7 (.D(Third), .en(write3), .clk(clk), .Q(current_line[23:16]));  // open: clr
  Register register_8 (.D(Fourth), .en(write4), .clk(clk), .Q(current_line[31:24]));  // open: clr
  Multiplexer #(.enable("false")) multiplexer_7 (.in0(wriite), .in1(two), .out(write2), .sel(wriite_val));
  Multiplexer #(.enable("false")) multiplexer_8 (.in0(wriite), .in1(four), .out(write4), .sel(wriite_val));
  Multiplexer #(.enable("false"), .select(2), .width(8)) multiplexer_9 (
    .in0(current_line[7:0]), .in1(current_line[15:8]), .in2(current_line[23:16]), .in3(current_line[31:24]),
    .out(byteRead), .sel(ofset));
  and and_1 (contain, cur_valid, comparator_1_eq);
  Comparator #(.width(7)) comparator_1 (.a(tag), .b(current_tag), .eq(comparator_1_eq));  // open: gt, lt

  // Other names for the same wires on the sheet: contains = contain; CpuTag[6:0] = tag; cur_age[1:0] = current_age;
  //   cur_dirty = isDirty; cur_tag[6:0] = current_tag; first_line[7:0] = LFM[7:0]; LineFromMem[31:0] = LFM;
  //   second_line[7:0] = LFM[15:8]; third_line[7:0] = LFM[23:16]; fourth_line[7:0] = LFM[31:24];
  //   line_one[7:0] = current_line[7:0]; lines[31:0] = current_line; line_two[7:0] = current_line[15:8];
  //   line_three[7:0] = current_line[23:16]; line_four[7:0] = current_line[31:24]; offset[1:0] = ofset;
  //   read[7:0] = byteRead; val_write = wriite_val; write = wriite
endmodule

module age_change (
  input  [1:0] cur_age,
  input  [1:0] agetochagne,
  input  [1:0] beginnVal,
  input  beginn,
  output [1:0] age_changed
);

  wire and_1_out, and_2_out, and_3_out, and_4_out, and_5_out, and_6_out, and_7_out, and_8_out, and_9_out,
       and_10_out, and_11_out, and_12_out, not_1_out, not_2_out, not_3_out, not_4_out, not_5_out;

  not not_1 (not_1_out, cur_age[1]);
  not not_2 (not_2_out, cur_age[0]);
  not not_3 (not_3_out, agetochagne[1]);
  not not_4 (not_4_out, agetochagne[0]);
  not not_5 (not_5_out, beginn);
  and and_1 (and_1_out, beginn, beginnVal[1]);
  and and_2 (and_2_out, not_1_out, cur_age[0], agetochagne[1], not_5_out);
  and and_3 (and_3_out, cur_age[1], not_3_out, not_5_out);
  and and_4 (and_4_out, cur_age[1], not_2_out, agetochagne[0], not_5_out);
  and and_5 (and_5_out, cur_age[1], cur_age[0], not_4_out, not_5_out);
  and and_6 (and_6_out, beginn, beginnVal[0]);
  and and_7 (and_7_out, not_1_out, not_2_out, agetochagne[0], not_5_out);
  and and_8 (and_8_out, not_1_out, not_2_out, agetochagne[1], not_5_out);
  and and_9 (and_9_out, not_2_out, agetochagne[1], agetochagne[0], not_5_out);
  and and_10 (and_10_out, cur_age[0], not_3_out, not_4_out, not_5_out);
  and and_11 (and_11_out, cur_age[1], cur_age[0], not_3_out, not_5_out);
  and and_12 (and_12_out, cur_age[1], cur_age[0], not_4_out, not_5_out);
  or or_1 (age_changed[1], and_1_out, and_2_out, and_3_out, and_4_out, and_5_out);
  or or_2 (age_changed[0], and_6_out, and_7_out, and_8_out, and_9_out, and_10_out, and_11_out, and_12_out);
endmodule

module FSM (
  input  three,
  input  two,
  input  one,
  input  Read,
  input  Write,
  input  Contains,
  input  olddirty,
  input  third,
  input  second,
  input  first,
  input  readd,
  input  writee,
  input  contain,
  input  old,
  output threee,
  output twoo,
  output onee,
  output intial,
  output ready,
  output readmem,
  output writemen,
  output writeStart,
  output write_val,
  output changeAge
);

  wire and_1_out, and_2_out, and_3_out, and_4_out, and_5_out, and_6_out, and_7_out, and_8_out, and_9_out,
       and_10_out, and_11_out, and_12_out, and_13_out, and_14_out, and_17_out, and_18_out, and_19_out,
       and_20_out, and_21_out, and_22_out, and_23_out, and_25_out, and_26_out, not_1_out, not_2_out,
       not_3_out, not_4_out, not_5_out, not_6_out, not_7_out, not_8_out, not_9_out, not_10_out, not_11_out,
       not_12_out;

  not not_1 (not_1_out, three);
  not not_2 (not_2_out, two);
  not not_3 (not_3_out, one);
  not not_4 (not_4_out, Read);
  not not_5 (not_5_out, Write);
  not not_6 (not_6_out, olddirty);
  not not_7 (not_7_out, third);
  not not_8 (not_8_out, second);
  not not_9 (not_9_out, first);
  not not_10 (not_10_out, readd);
  not not_11 (not_11_out, writee);
  not not_12 (not_12_out, contain);
  and and_1 (and_1_out, two, not_4_out, Write, not_6_out);
  and and_2 (and_2_out, two, not_4_out, Write, Contains);
  and and_3 (and_3_out, two, not_3_out, Read, not_5_out, not_6_out);
  and and_4 (and_4_out, two, not_3_out, Read, not_5_out, Contains);
  and and_5 (and_5_out, not_1_out, two, one);
  and and_6 (and_6_out, three, not_3_out);
  and and_7 (and_7_out, three, two, not_4_out);
  and and_8 (and_8_out, not_1_out, one);
  and and_9 (and_9_out, two, not_3_out);
  and and_10 (and_10_out, not_2_out, not_3_out);
  and and_11 (and_11_out, not_3_out, not_4_out, Write, olddirty);
  and and_12 (and_12_out, not_3_out, not_4_out, Write, Contains);
  and and_13 (and_13_out, not_3_out, Read, not_5_out, olddirty);
  and and_14 (and_14_out, not_3_out, Read, not_5_out, Contains);
  and and_15 (intial, not_7_out, not_8_out, not_9_out);
  and and_16 (ready, not_7_out, not_8_out, first);
  and and_17 (and_17_out, third, second, not_9_out, not_10_out, writee, not_12_out);
  and and_18 (and_18_out, third, second, not_9_out, readd, not_11_out, not_12_out);
  and and_19 (and_19_out, not_7_out, second, first, not_10_out, writee, not_12_out, old);
  and and_20 (and_20_out, not_7_out, second, first, readd, not_11_out, not_12_out, old);
  and and_21 (and_21_out, third, not_8_out, first, not_10_out, writee);
  and and_22 (and_22_out, third, second, not_9_out, not_10_out, writee, not_12_out);
  and and_23 (and_23_out, third, second, not_9_out, readd, not_11_out, not_12_out);
  and and_24 (write_val, third, not_8_out, first, not_10_out, writee);
  and and_25 (and_25_out, not_7_out, not_8_out, not_9_out);
  and and_26 (and_26_out, third, second, first);
  or or_1 (threee, and_1_out, and_2_out, and_3_out, and_4_out, and_5_out, and_6_out, and_7_out);
  or or_2 (twoo, and_8_out, and_9_out);
  or or_3 (onee, and_10_out, and_11_out, and_12_out, and_13_out, and_14_out, three);
  or or_4 (readmem, and_17_out, and_18_out);
  or or_5 (writemen, and_19_out, and_20_out);
  or or_6 (writeStart, and_21_out, and_22_out, and_23_out);
  or or_7 (changeAge, and_25_out, and_26_out);
endmodule
