// Logisim project 3BitMultiplier.circ as structural Verilog: 1 circuit, main circuit main
module main (
  input  [2:0] A,
  input  [2:0] B,
  output [5:0] Product
);

  wire [5:0] A_Ext, adder_1_out, and_1_out, and_2_out, and_3_out, B0_Ext, B1_Ext, B2_Ext, shifter_1_out,
       shifter_2_out, shifter_3_out;

  assign B2_Ext = {{5{B[2]}}, B[2]};  // Bit_Extender bit_extender_1
  assign B1_Ext = {{5{B[1]}}, B[1]};  // Bit_Extender bit_extender_2
  assign B0_Ext = {{5{B[0]}}, B[0]};  // Bit_Extender bit_extender_3
  assign A_Ext = {{3{1'b0}}, A};  // Bit_Extender bit_extender_4
  Shifter #(.width(6)) shifter_1 (.in(A_Ext), .\dist (3'b000), .out(shifter_1_out));
  assign and_1_out = B0_Ext & shifter_1_out;  // AND_Gate and_1, 6 bits wide
  Shifter #(.width(6)) shifter_2 (.in(A_Ext), .\dist (3'b001), .out(shifter_2_out));
  // Probe on A
  // Probe on B
  // Probe on Product
  // Probe on and_1_out
  assign and_2_out = B1_Ext & shifter_2_out;  // AND_Gate and_2, 6 bits wide
  // Probe on and_2_out
  // Probe on adder_1_out
  Adder #(.width(6)) adder_1 (.a(and_1_out), .b(and_2_out), .out(adder_1_out), .cin(1'b0));  // open: cout
  Shifter #(.width(6)) shifter_3 (.in(A_Ext), .\dist (3'b010), .out(shifter_3_out));
  assign and_3_out = B2_Ext & shifter_3_out;  // AND_Gate and_3, 6 bits wide
  // Probe on and_3_out
  Adder #(.width(6)) adder_2 (.a(adder_1_out), .b(and_3_out), .out(Product), .cin(1'b0));  // open: cout
endmodule
