// Logisim project Adders.circ as structural Verilog: 5 circuits, main circuit HalfAdder
module HalfAdder (
  input  A,
  input  B,
  output Sum,
  output CarryOut
);

  xor xor_1 (Sum, A, B);
  and and_1 (CarryOut, A, B);
endmodule

module FullAdder (
  input  A,
  input  B,
  input  CarryIn,
  output Sum,
  output CarryOut
);

  wire and_1_out, and_2_out, and_3_out;

  and and_1 (and_1_out, A, B);
  and and_2 (and_2_out, A, CarryIn);
  and and_3 (and_3_out, B, CarryIn);
  xor xor_1 (Sum, A, B, CarryIn);
  or or_1 (CarryOut, and_1_out, and_2_out, and_3_out);
endmodule

module FullAdderLessHardware (
  input  A,
  input  B,
  input  Cin,
  output Sum,
  output Cout
);

  wire and_1_out, and_2_out, xor_1_out;

  xor xor_1 (xor_1_out, A, B);
  and and_1 (and_1_out, A, B);
  xor xor_2 (Sum, Cin, xor_1_out);
  and and_2 (and_2_out, xor_1_out, Cin);
  or or_1 (Cout, and_2_out, and_1_out);
endmodule

module RippleCarryAdder (
  input  [2:0] A,
  input  [2:0] B,
  input  CarryIn,
  output [2:0] Sum,
  output CarryOut
);

  wire fulladder_1_carryout, fulladder_2_carryout;

  FullAdder fulladder_1 (.A(A[0]), .B(B[0]), .CarryIn(CarryIn), .Sum(Sum[0]), .CarryOut(fulladder_1_carryout));
  FullAdder fulladder_2 (
    .A(A[1]), .B(B[1]), .CarryIn(fulladder_1_carryout), .Sum(Sum[1]), .CarryOut(fulladder_2_carryout));
  // Probe on A
  // Probe on B
  // Probe on Sum
  // Probe on CarryOut
  FullAdder fulladder_3 (.A(A[2]), .B(B[2]), .CarryIn(fulladder_2_carryout), .Sum(Sum[2]), .CarryOut(CarryOut));

  // Other names for the same wires on the sheet: Cin = CarryIn; Cout = CarryOut; S0 = Sum[0]; S1 = Sum[1];
  //   S2 = Sum[2]
endmodule

module Subtractor (
  input  [2:0] A,
  input  [2:0] B,
  output [2:0] A___B
);

  wire [2:0] not_1_out;

  assign not_1_out = ~B;  // NOT_Gate not_1, 3 bits wide
  Adder #(.width(3)) adder_1 (.a(A), .b(not_1_out), .out(A___B), .cin(1'b1));  // open: cout
  // Probe on A
  // Probe on B
  // Probe on A___B
endmodule
