// Logisim project CombinationalBuildingBlocksImplementations.circ as structural Verilog: 9 circuits, main circuit mux
module mux (
  input  S,
  input  D0,
  input  D1,
  input  S1,
  input  S0,
  output Out
);

  wire [2:0] multiplexer_2_out;

  Multiplexer #(.enable("false")) multiplexer_1 (.in0(D0), .in1(D1), .out(Out), .sel(S));
  // Probe on multiplexer_2_out
  Multiplexer #(.select(2), .width(3), .disabled(0), .enable("false")) multiplexer_2 (
    .in0(3'b111), .in1(3'b101), .in2(3'b110), .out(multiplexer_2_out), .sel({S1, S0}));  // open: in3
endmodule

module _2_1MultiplexerImp (
  input  S,
  input  D1,
  input  D0,
  output Out
);

  wire and_1_out, and_2_out, nS;

  not not_1 (nS, S);
  and and_1 (and_1_out, S, D1);
  and and_2 (and_2_out, nS, D0);
  or or_1 (Out, and_1_out, and_2_out);
endmodule

module _4_1MultiplexerImp (
  input  S1,
  input  S0,
  input  D3,
  input  D2,
  input  D1,
  input  D0,
  output Out
);

  wire and_1_out, and_2_out, and_3_out, and_4_out, not_1_out, not_2_out, not_3_out, not_4_out;

  not not_1 (not_1_out, S1);
  not not_2 (not_2_out, S0);
  not not_3 (not_3_out, S1);
  not not_4 (not_4_out, S0);
  and and_1 (and_1_out, not_1_out, not_2_out, D0);
  and and_2 (and_2_out, not_3_out, S0, D1);
  and and_3 (and_3_out, S1, not_4_out, D2);
  and and_4 (and_4_out, S1, S0, D3);
  or or_1 (Out, and_1_out, and_2_out, and_3_out, and_4_out);
endmodule

module _4_1MuxOfMuxes (
  input  [1:0] S,
  input  D3,
  input  D2,
  input  D1,
  input  D0,
  output Out
);

  wire multiplexer_1_out, multiplexer_2_out;

  Multiplexer #(.enable("false")) multiplexer_1 (.in0(D0), .in1(D1), .out(multiplexer_1_out), .sel(S[0]));
  Multiplexer #(.enable("false")) multiplexer_2 (.in0(D2), .in1(D3), .out(multiplexer_2_out), .sel(S[0]));
  Multiplexer #(.enable("false")) multiplexer_3 (
    .in0(multiplexer_1_out), .in1(multiplexer_2_out), .out(Out), .sel(S[1]));
endmodule

module demux (
  input  S,
  input  D,
  output Out0,
  output Out1
);

  Demultiplexer #(.enable("false")) demultiplexer_1 (.out0(Out0), .out1(Out1), .in(D), .sel(S));
endmodule

module demuxImp (
  input  S,
  input  D,
  output Out1,
  output Out0
);

  wire not_1_out;

  and and_1 (Out1, S, D);
  not not_1 (not_1_out, S);
  and and_2 (Out0, not_1_out, D);
endmodule

module decoder (
  input  [1:0] X,
  output Out0,
  output Out1,
  output Out2,
  output Out3
);

  Decoder #(.select(2), .enable("false")) decoder_1 (.out0(Out0), .out1(Out1), .out2(Out2), .out3(Out3), .sel(X));
endmodule

module XOR_muxStyle (
  input  A,
  input  B,
  output Out
);

  Multiplexer #(.select(2), .enable("false")) multiplexer_1 (
    .in0(1'b0), .in1(1'b1), .in2(1'b1), .in3(1'b0), .out(Out), .sel({A, B}));
endmodule

// Output
module XOR_DecoderStyle (
  input  A,
  input  B,
  output out_3
);

  wire decoder_1_out1, decoder_1_out2;

  Decoder #(.select(2), .enable("false")) decoder_1 (
    .out1(decoder_1_out1), .out2(decoder_1_out2), .sel({A, B}));  // open: out0, out3
  or or_1 (out_3, decoder_1_out1, decoder_1_out2);
endmodule
