// Logisim project EvolvedBuildingBlockImplementations.circ as structural Verilog
module main (
);

  full_adder full_adder_1 ();  // open: A, B, Cin, sum, Cout
endmodule

module mux2 (
  input  SelectIn,
  input  D0In,
  input  D1In,
  output mux_out
);

  wire and_1_out, and_2_out;

  Multiplexer #(.enable("false")) multiplexer_1 ();  // open: in0, in1, out, sel
  and and_1 (and_1_out, SelectIn, D1In);
  and and_2 (and_2_out, ~SelectIn, D0In);  // AND_Gate
  or or_1 (mux_out, and_1_out, and_2_out);

  // Other names for the same wires on the sheet: D0 = D0In; D1 = D1In; select_t = SelectIn
endmodule

module mux4 (
  input  [1:0] SelectIn,
  input  D3In,
  input  D2In,
  input  D1In,
  input  D0in,
  output result
);

  wire multiplexer_1_out, multiplexer_2_out;

  Multiplexer #(.enable("false")) multiplexer_1 (.in0(D0in), .in1(D1In), .out(multiplexer_1_out), .sel(SelectIn[0]));
  Multiplexer #(.enable("false")) multiplexer_2 (.in0(D2In), .in1(D3In), .out(multiplexer_2_out), .sel(SelectIn[0]));
  Multiplexer #(.enable("false")) multiplexer_3 (
    .in0(multiplexer_1_out), .in1(multiplexer_2_out), .out(result), .sel(SelectIn[1]));

  // Other names for the same wires on the sheet: D0 = D0in; D1 = D1In; D2 = D2In; D3 = D3In; S0 = SelectIn[0];
  //   S1 = SelectIn[1]
endmodule

module decoder_example (
  input  [1:0] in_1,
  input  in_2
);

  wire decoder_1_out0, decoder_1_out1, decoder_1_out2, decoder_1_out3;

  Decoder #(.select(2)) decoder_1 (
    .out0(decoder_1_out0), .out1(decoder_1_out1), .out2(decoder_1_out2), .out3(decoder_1_out3), .sel(in_1),
    .en(in_2));
endmodule

module DecoderImplemenentation (
  input  [1:0] in_1,
  output out_2,
  output out_3,
  output out_4,
  output out_5
);

  and and_1 (out_2, ~in_1[0], ~in_1[1]);  // AND_Gate
  and and_2 (out_3, in_1[0], ~in_1[1]);  // AND_Gate
  and and_3 (out_4, ~in_1[0], in_1[1]);  // AND_Gate
  and and_4 (out_5, in_1[0], in_1[1]);

  // Other names for the same wires on the sheet: b0 = in_1[0]; b1 = in_1[1]
endmodule

module demux (
  input  in_1,
  input  [1:0] in_2,
  output out_3,
  output out_4,
  output out_5,
  output out_6
);

  wire and_1_out, and_2_out, and_5_out, and_6_out;

  and and_1 (and_1_out, ~in_2[0], ~in_2[1]);  // AND_Gate
  and and_2 (and_2_out, in_2[0], ~in_2[1]);  // AND_Gate
  and and_3 (out_3, and_1_out, in_1);
  and and_4 (out_4, and_2_out, in_1);
  and and_5 (and_5_out, ~in_2[0], in_2[1]);  // AND_Gate
  and and_6 (and_6_out, in_2[0], in_2[1]);
  and and_7 (out_5, and_5_out, in_1);
  and and_8 (out_6, and_6_out, in_1);

  // Other names for the same wires on the sheet: data = in_1; b0 = in_2[0]; b1 = in_2[1]
endmodule

module full_adder (
  input  A,
  input  B,
  input  Cin,
  output sum,
  output Cout
);

  wire and_1_out, and_2_out, xor_1_out;

  xor xor_1 (xor_1_out, A, B);
  and and_1 (and_1_out, A, B);
  and and_2 (and_2_out, xor_1_out, Cin);
  xor xor_2 (sum, xor_1_out, Cin);
  or or_1 (Cout, and_1_out, and_2_out);
endmodule

module Rippleadder3 (
  input  [2:0] A,
  input  [2:0] B,
  input  TheCin,
  output [2:0] Sum,
  output CarryOut
);

  wire full_adder_1_cout, full_adder_2_cout;

  // Probe on B
  // Probe on B
  // Probe on A
  // Probe on A
  full_adder full_adder_1 (.A(A[0]), .B(B[0]), .Cin(TheCin), .sum(Sum[0]), .Cout(full_adder_1_cout));
  // Probe on Sum
  // Probe on Sum
  // Probe on {CarryOut, Sum}
  full_adder full_adder_2 (.A(A[1]), .B(B[1]), .Cin(full_adder_1_cout), .sum(Sum[1]), .Cout(full_adder_2_cout));
  // Probe on {CarryOut, Sum}
  full_adder full_adder_3 (.A(A[2]), .B(B[2]), .Cin(full_adder_2_cout), .sum(Sum[2]), .Cout(CarryOut));

  // Other names for the same wires on the sheet: S0 = Sum[0]; S1 = Sum[1]; S2 = Sum[2]; Cin = TheCin
endmodule

module Mux3Bits (
  input  Sin,
  input  [2:0] Data0In,
  input  [2:0] Data1In,
  output [2:0] Result
);

  wire [2:0] multiplexer_4_out;

  Multiplexer #(.enable("false")) multiplexer_1 (.in0(Data0In[0]), .in1(Data1In[0]), .out(Result[0]), .sel(Sin));
  Multiplexer #(.enable("false")) multiplexer_2 (.in0(Data0In[1]), .in1(Data1In[1]), .out(Result[1]), .sel(Sin));
  Multiplexer #(.enable("false")) multiplexer_3 (.in0(Data0In[2]), .in1(Data1In[2]), .out(Result[2]), .sel(Sin));
  Multiplexer #(.enable("false"), .width(3)) multiplexer_4 (
    .in0(Data0In), .in1(Data1In), .out(multiplexer_4_out), .sel(Sin));
  // Probe on multiplexer_4_out

  // Other names for the same wires on the sheet: D0[2:0] = Data0In; D00 = Data0In[0]; D01 = Data0In[1];
  //   D02 = Data0In[2]; D1[2:0] = Data1In; D10 = Data1In[0]; D11 = Data1In[1]; D12 = Data1In[2]; S = Sin
endmodule

module SubCirc3 (
  input  [2:0] A,
  input  [2:0] B
);

  wire [2:0] not_1_out, rippleadder3_1_sum;

  // Probe on B
  // Probe on A
  // Probe on A
  assign not_1_out = ~B;  // NOT_Gate not_1, 3 bits wide
  Rippleadder3 rippleadder3_1 (.A(A), .B(not_1_out), .TheCin(1'b1), .Sum(rippleadder3_1_sum));  // open: CarryOut
  // Probe on rippleadder3_1_sum
endmodule

module Multiplier4 (
  input  [3:0] AIn,
  input  [3:0] Bin,
  output [7:0] Product
);

  wire [3:0] bit_extender_1_out, bit_extender_2_out, Partial0, Partial1, Partial2, Partial3;
  wire [6:0] adder_1_out, adder_2_out, bit_extender_3_out, bit_extender_4_out, bit_extender_5_out;
  wire [7:7] adder_1_cout, adder_2_cout;

  // Probe on AIn
  // Probe on Bin
  assign bit_extender_1_out = {{3{Bin[2]}}, Bin[2]};  // Bit_Extender bit_extender_1
  assign bit_extender_2_out = {{3{Bin[3]}}, Bin[3]};  // Bit_Extender bit_extender_2
  Multiplexer #(.enable("false"), .width(4)) multiplexer_1 (.in0(4'b0000), .in1(AIn), .out(Partial0), .sel(Bin[0]));
  assign Partial1 = AIn & {4{Bin[1]}};  // AND_Gate and_1, 4 bits wide
  assign Partial2 = AIn & bit_extender_1_out;  // AND_Gate and_2, 4 bits wide
  assign Partial3 = AIn & bit_extender_2_out;  // AND_Gate and_3, 4 bits wide
  // Probe on bit_extender_3_out
  assign bit_extender_3_out = {{3{1'b0}}, Partial0};  // Bit_Extender bit_extender_3
  assign bit_extender_4_out = {{2{1'b0}}, {Partial1, 1'b0}};  // Bit_Extender bit_extender_4
  // Probe on bit_extender_4_out
  // Probe on bit_extender_5_out
  assign bit_extender_5_out = {{1{1'b0}}, {Partial2, 2'b00}};  // Bit_Extender bit_extender_5
  // Probe on {Partial3, 3'b000}
  Adder #(.width(7)) adder_1 (
    .a(bit_extender_3_out), .b(bit_extender_4_out), .out(adder_1_out), .cout(adder_1_cout[7]));  // open: cin
  Adder #(.width(7)) adder_2 (
    .a(bit_extender_5_out), .b({Partial3, 3'b000}), .out(adder_2_out), .cout(adder_2_cout[7]));  // open: cin
  Adder adder_3 (
    .a({adder_1_cout[7], adder_1_out}), .b({adder_2_cout[7], adder_2_out}), .out(Product));  // open: cin, cout
  // Probe on Product

  // Other names for the same wires on the sheet: B1 = Bin[1]; A[3:0] = AIn; B0 = Bin[0]; B2 = Bin[2]; B3 = Bin[3]
endmodule
