// Logisim project MuxExample.circ as structural Verilog: 1 circuit, main circuit main
module main (
  input  [1:0] OpSelectIn,
  input  [7:0] Ain,
  input  NegAIn,
  input  [7:0] Bin,
  input  NegBIn,
  output [7:0] out_6
);

  wire [3:0] adder_2_out, bitadder_1_out, bitadder_2_out;
  wire [7:0] A, adder_1_out, B, bit_extender_1_out, divider_1_out, multiplier_1_out, negator_1_out,
       negator_2_out;

  Multiplexer #(.enable("false"), .width(8)) multiplexer_1 (.in0(Ain), .in1(negator_1_out), .out(A), .sel(NegAIn));
  Negator negator_1 (.in(Ain), .out(negator_1_out));
  Multiplexer #(.enable("false"), .width(8)) multiplexer_2 (.in0(Bin), .in1(negator_2_out), .out(B), .sel(NegBIn));
  Negator negator_2 (.in(Bin), .out(negator_2_out));
  Adder adder_1 (.a(A), .b(B), .out(adder_1_out));  // open: cin, cout
  Multiplier multiplier_1 (.a(A), .b(B), .out(multiplier_1_out));  // open: cin, cout
  Divider divider_1 (.a(A), .b(B), .out(divider_1_out));  // open: upper, rem
  BitAdder bitadder_1 (.in0(A), .out(bitadder_1_out));
  BitAdder bitadder_2 (.in0(B), .out(bitadder_2_out));
  Adder #(.width(4)) adder_2 (.a(bitadder_1_out), .b(bitadder_2_out), .out(adder_2_out));  // open: cin, cout
  assign bit_extender_1_out = {{4{1'b0}}, adder_2_out};  // Bit_Extender bit_extender_1
  Multiplexer #(.enable("false"), .select(2), .width(8)) multiplexer_3 (
    .in0(adder_1_out), .in1(multiplier_1_out), .in2(divider_1_out), .in3(bit_extender_1_out), .out(out_6),
    .sel(OpSelectIn));
  // Probe on out_6

  // Other names for the same wires on the sheet: NegA = NegAIn; NegB = NegBIn; OpSelect[1:0] = OpSelectIn;
  //   PreA[7:0] = Ain; PreB[7:0] = Bin
endmodule
