// Logisim project adder4.circ as structural Verilog: 6 circuits, main circuit implementation
module implementation (
  input  [3:0] Ain,
  input  [3:0] Bin,
  input  Cinin,
  output [3:0] Sum_Out,
  output Carry_Out
);

  wire C0, C1, C2, G0, G1, G2, G3, P0, P1, P2, P3;

  GG gg_1 (.A(Ain[0]), .B(Bin[0]), .G(G0));
  PP pp_1 (.A(Ain[0]), .B(Bin[0]), .P(P0));
  GG gg_2 (.A(Ain[1]), .B(Bin[1]), .G(G1));
  PP pp_2 (.A(Ain[1]), .B(Bin[1]), .P(P1));
  GG gg_3 (.A(Ain[2]), .B(Bin[2]), .G(G2));
  PP pp_3 (.A(Ain[2]), .B(Bin[2]), .P(P2));
  GG gg_4 (.A(Ain[3]), .B(Bin[3]), .G(G3));
  PP pp_4 (.A(Ain[3]), .B(Bin[3]), .P(P3));
  CI ci_1 (.G(G0), .P(P0), .C(Cinin), .CC(C0));
  CI ci_2 (.G(G1), .P(P1), .C(C0), .CC(C1));
  CI ci_3 (.G(G2), .P(P2), .C(C1), .CC(C2));
  CI ci_4 (.G(G3), .P(P3), .C(C2), .CC(Carry_Out));
  SS ss_1 (.A(Ain[0]), .B(Bin[0]), .C(Cinin), .S(Sum_Out[0]));
  SS ss_2 (.A(Ain[1]), .B(Bin[1]), .C(C0), .S(Sum_Out[1]));
  SS ss_3 (.A(Ain[2]), .B(Bin[2]), .C(C1), .S(Sum_Out[2]));
  SS ss_4 (.A(Ain[3]), .B(Bin[3]), .C(C2), .S(Sum_Out[3]));

  // Other names for the same wires on the sheet: A[3:0] = Ain; A0 = Ain[0]; A1 = Ain[1]; A2 = Ain[2]; A3 = Ain[3];
  //   B[3:0] = Bin; B0 = Bin[0]; B1 = Bin[1]; B2 = Bin[2]; B3 = Bin[3]; C3 = Carry_Out; Cin = Cinin; S0 = Sum_Out[0];
  //   Sum[3:0] = Sum_Out; S1 = Sum_Out[1]; S2 = Sum_Out[2]; S3 = Sum_Out[3]
endmodule

module fulladder (
  input  A,
  input  B,
  input  CarryIn,
  output Sum,
  output CarryOut
);

  wire and_1_out, and_2_out, and_3_out;

  xor xor_1 (Sum, A, B, CarryIn);
  and and_1 (and_1_out, A, B);
  and and_2 (and_2_out, A, CarryIn);
  and and_3 (and_3_out, B, CarryIn);
  or or_1 (CarryOut, and_1_out, and_2_out, and_3_out);
endmodule

module PP (
  input  A,
  input  B,
  output P
);

  xor xor_1 (P, A, B);
endmodule

module GG (
  input  A,
  input  B,
  output G
);

  and and_1 (G, A, B);
endmodule

module CI (
  input  G,
  input  P,
  input  C,
  output CC
);

  wire and_1_out;

  or or_1 (CC, G, and_1_out);
  and and_1 (and_1_out, P, C);
endmodule

module SS (
  input  A,
  input  B,
  input  C,
  output S
);

  wire xor_1_out;

  xor xor_1 (xor_1_out, A, B);
  xor xor_2 (S, xor_1_out, C);
endmodule
