// Logisim project bitcounter.circ as structural Verilog: 2 circuits, main circuit implementation
module implementation (
  input  [7:0] BitsIn,
  input  CountZerosIn,
  output [3:0] BitCountOut
);

  wire [3:0] adder_1_out, adder_2_out, adder_3_out, adder_4_out, adder_5_out, adder_6_out, ans,
       bit_extender_1_out, bit_extender_2_out, bit_extender_3_out, bit_extender_4_out, bit_extender_5_out,
       bit_extender_6_out, bit_extender_7_out, bit_extender_8_out;

  assign bit_extender_1_out = {{3{1'b0}}, BitsIn[0]};  // Bit_Extender bit_extender_1
  assign bit_extender_2_out = {{3{1'b0}}, BitsIn[1]};  // Bit_Extender bit_extender_2
  assign bit_extender_3_out = {{3{1'b0}}, BitsIn[2]};  // Bit_Extender bit_extender_3
  assign bit_extender_4_out = {{3{1'b0}}, BitsIn[3]};  // Bit_Extender bit_extender_4
  assign bit_extender_5_out = {{3{1'b0}}, BitsIn[4]};  // Bit_Extender bit_extender_5
  assign bit_extender_6_out = {{3{1'b0}}, BitsIn[5]};  // Bit_Extender bit_extender_6
  assign bit_extender_7_out = {{3{1'b0}}, BitsIn[6]};  // Bit_Extender bit_extender_7
  assign bit_extender_8_out = {{3{1'b0}}, BitsIn[7]};  // Bit_Extender bit_extender_8
  Adder #(.width(4)) adder_1 (.a(bit_extender_1_out), .b(bit_extender_2_out), .out(adder_1_out));  // open: cin, cout
  Adder #(.width(4)) adder_2 (.a(bit_extender_3_out), .b(bit_extender_4_out), .out(adder_2_out));  // open: cin, cout
  Adder #(.width(4)) adder_3 (.a(bit_extender_5_out), .b(bit_extender_6_out), .out(adder_3_out));  // open: cin, cout
  Adder #(.width(4)) adder_4 (.a(bit_extender_7_out), .b(bit_extender_8_out), .out(adder_4_out));  // open: cin, cout
  Adder #(.width(4)) adder_5 (.a(adder_1_out), .b(adder_2_out), .out(adder_5_out));  // open: cin, cout
  Adder #(.width(4)) adder_6 (.a(adder_3_out), .b(adder_4_out), .out(adder_6_out));  // open: cin, cout
  Adder #(.width(4)) adder_7 (.a(adder_5_out), .b(adder_6_out), .out(ans));  // open: cin, cout
  swap swap_1 (.a(ans[3]), .b(ans[2]), .c(ans[1]), .d(ans[0]), .clock(CountZerosIn), .sum(BitCountOut));

  // Other names for the same wires on the sheet: BitCount[3:0] = BitCountOut; b0 = BitsIn[0]; Bits[7:0] = BitsIn;
  //   b1 = BitsIn[1]; b2 = BitsIn[2]; b3 = BitsIn[3]; b4 = BitsIn[4]; b5 = BitsIn[5]; b6 = BitsIn[6]; b7 = BitsIn[7];
  //   CountZeros = CountZerosIn
endmodule

module swap (
  input  a,
  input  b,
  input  c,
  input  d,
  input  clock,
  output [3:0] sum
);

  wire and_1_out, and_2_out, and_3_out, and_4_out, and_5_out, and_6_out, and_7_out, and_8_out, and_9_out,
       and_10_out, and_11_out, and_12_out, not_1_out, not_2_out, not_3_out, not_4_out, not_5_out;

  not not_1 (not_1_out, a);
  not not_2 (not_2_out, b);
  not not_3 (not_3_out, c);
  not not_4 (not_4_out, d);
  not not_5 (not_5_out, clock);
  and and_1 (and_1_out, not_1_out, not_2_out, not_3_out, not_4_out, clock);
  or or_1 (sum[3], and_1_out, and_2_out);
  and and_2 (and_2_out, a, not_2_out, not_3_out, not_4_out, not_5_out);
  and and_3 (and_3_out, not_2_out, d, clock);
  and and_4 (and_4_out, not_2_out, c, clock);
  and and_5 (and_5_out, not_1_out, b, not_5_out);
  and and_6 (and_6_out, b, not_3_out, not_4_out);
  and and_7 (and_7_out, a, not_2_out, d);
  and and_8 (and_8_out, a, not_2_out, c);
  and and_9 (and_9_out, not_3_out, d, clock);
  and and_10 (and_10_out, not_1_out, c, not_5_out);
  and and_11 (and_11_out, c, not_4_out);
  and and_12 (and_12_out, a, not_3_out, d);
  or or_2 (sum[2], and_3_out, and_4_out, and_5_out, and_6_out, and_7_out, and_8_out);
  or or_3 (sum[1], and_9_out, and_10_out, and_11_out, and_12_out);

  assign sum[0] = d;
endmodule
