// Logisim project shifter.circ as structural Verilog: 3 circuits, main circuit implementation
module implementation (
  input  IsRightShiftIn,
  input  IsArithmeticIn,
  input  [1:0] ShiftAmountIn,
  input  [2:0] NumberIn,
  input  in_5,
  input  in_6,
  output [2:0] ShiftedNumberOut
);

  wire [2:0] muux_1_a2, right_1_a2;

  muux muux_1 (
    .b0(NumberIn[2]), .b1(NumberIn[1]), .b2(NumberIn[0]), .zero(in_5), .shift(ShiftAmountIn),
    .a0(muux_1_a2[2]), .a1(muux_1_a2[1]), .a2(muux_1_a2[0]));
  Right right_1 (
    .b0(NumberIn[2]), .b1(NumberIn[1]), .b2(NumberIn[0]), .zero(in_6), .AorL(IsArithmeticIn),
    .shift(ShiftAmountIn), .a0(right_1_a2[2]), .a1(right_1_a2[1]), .a2(right_1_a2[0]));
  Multiplexer #(.enable("false"), .width(3)) multiplexer_1 (
    .in0(muux_1_a2), .in1(right_1_a2), .out(ShiftedNumberOut), .sel(IsRightShiftIn));

  // Other names for the same wires on the sheet: IsArithmetic = IsArithmeticIn; IsRightShift = IsRightShiftIn;
  //   a0 = NumberIn[0]; Number[2:0] = NumberIn; a1 = NumberIn[1]; a2 = NumberIn[2]; ShiftAmount[1:0] = ShiftAmountIn;
  //   ShiftedNumber[2:0] = ShiftedNumberOut
endmodule

module muux (
  input  b0,
  input  b1,
  input  b2,
  input  zero,
  input  [1:0] shift,
  output a0,
  output a1,
  output a2
);

  wire and_1_out, and_2_out, and_3_out, and_4_out, and_5_out, and_6_out, and_7_out, and_8_out, not_1_out,
       not_2_out, not_3_out;

  not not_1 (not_1_out, zero);
  not not_2 (not_2_out, shift[1]);
  not not_3 (not_3_out, shift[0]);
  and and_1 (and_1_out, b2, shift[1], not_3_out);
  and and_2 (and_2_out, b1, not_2_out, shift[0]);
  and and_3 (and_3_out, b0, not_2_out, not_3_out);
  and and_4 (and_4_out, b2, not_2_out, shift[0]);
  and and_5 (and_5_out, b1, not_2_out, not_3_out);
  and and_6 (and_6_out, b2, not_1_out, not_2_out, not_3_out);
  and and_7 (and_7_out, b1, b2, not_2_out, not_3_out);
  and and_8 (and_8_out, b0, b2, not_2_out, not_3_out);
  or or_1 (a0, and_1_out, and_2_out, and_3_out);
  or or_2 (a1, and_4_out, and_5_out);
  or or_3 (a2, and_6_out, and_7_out, and_8_out);
endmodule

module Right (
  input  b0,
  input  b1,
  input  b2,
  input  zero,
  input  AorL,
  input  [1:0] shift,
  output a0,
  output a1,
  output a2
);

  wire and_1_out, and_2_out, and_3_out, and_4_out, and_5_out, and_6_out, and_7_out, and_8_out, and_9_out,
       and_10_out, and_11_out, and_12_out, and_13_out, not_1_out, not_2_out;

  not not_1 (not_1_out, shift[1]);
  not not_2 (not_2_out, shift[0]);
  and and_1 (and_1_out, zero, AorL, shift[0]);
  and and_2 (and_2_out, zero, AorL, shift[1]);
  and and_3 (and_3_out, b0, not_1_out, not_2_out);
  and and_4 (and_4_out, b0, AorL);
  and and_5 (and_5_out, zero, AorL, shift[1]);
  and and_6 (and_6_out, b1, not_1_out, not_2_out);
  and and_7 (and_7_out, b0, not_1_out, shift[0]);
  and and_8 (and_8_out, b0, AorL, shift[1]);
  and and_9 (and_9_out, zero, AorL, shift[1], shift[0]);
  and and_10 (and_10_out, b2, not_1_out, not_2_out);
  and and_11 (and_11_out, b1, not_1_out, shift[0]);
  and and_12 (and_12_out, b0, shift[1], not_2_out);
  and and_13 (and_13_out, b0, AorL, shift[1]);
  or or_1 (a0, and_1_out, and_2_out, and_3_out, and_4_out);
  or or_2 (a1, and_5_out, and_6_out, and_7_out, and_8_out);
  or or_3 (a2, and_9_out, and_10_out, and_11_out, and_12_out, and_13_out);
endmodule
