// Logisim project FourBitParity.circ as structural Verilog: 3 circuits, main circuit implementation
module implementation (
  input  EnableIn,
  input  InputBitIn,
  input  ClkIn,
  output IsEvenOut
);

  wire [1:0] check_1_flag_out, register_3_q;
  wire [2:0] check_1_fllagfive, register_2_q;
  wire [3:0] add_1_outstate, outt;

  Register #(.width(4)) register_1 (.D(add_1_outstate), .en(EnableIn), .clk(ClkIn), .Q(outt));  // open: clr
  Register #(.width(3)) register_2 (.D(check_1_fllagfive), .en(EnableIn), .clk(ClkIn), .Q(register_2_q));  // open: clr
  Register #(.width(2)) register_3 (.D(check_1_flag_out), .en(EnableIn), .clk(ClkIn), .Q(register_3_q));  // open: clr
  add add_1 (.inn(InputBitIn), .instate(outt), .outstate(add_1_outstate));
  check check_1 (
    .outt(outt), .flagfive(register_2_q), .flag_in(register_3_q), .flag_out(check_1_flag_out),
    .fllagfive(check_1_fllagfive), .even(IsEvenOut));

  // Other names for the same wires on the sheet: ans = IsEvenOut; Clk = ClkIn; Enable = EnableIn;
  //   InputBit = InputBitIn
endmodule

module add (
  input  inn,
  input  [3:0] instate,
  output [3:0] outstate
);


  assign outstate = {instate[2:0], inn};
endmodule

module check (
  input  [3:0] outt,
  input  [2:0] flagfive,
  input  [1:0] flag_in,
  output [1:0] flag_out,
  output [2:0] fllagfive,
  output even
);

  wire and_1_out, and_2_out, and_3_out, and_4_out, and_5_out, and_6_out, and_7_out, and_8_out, and_9_out,
       and_10_out, and_11_out, and_12_out, and_13_out, and_14_out, and_15_out, and_16_out, and_17_out,
       and_18_out, and_19_out, and_20_out, and_21_out, and_22_out, and_23_out, and_24_out, and_25_out,
       and_26_out, and_28_out, and_29_out, and_30_out, not_1_out, not_2_out, not_3_out, not_4_out, not_5_out,
       not_6_out, not_7_out, not_8_out, not_9_out;

  not not_1 (not_1_out, outt[3]);
  not not_2 (not_2_out, outt[2]);
  not not_3 (not_3_out, outt[1]);
  not not_4 (not_4_out, outt[0]);
  not not_5 (not_5_out, flagfive[2]);
  not not_6 (not_6_out, flagfive[1]);
  not not_7 (not_7_out, flagfive[0]);
  not not_8 (not_8_out, flag_in[1]);
  not not_9 (not_9_out, flag_in[0]);
  and and_1 (and_1_out, not_1_out, not_2_out, not_3_out, not_4_out, flagfive[2], not_6_out, not_7_out, not_8_out, not_9_out);
  and and_2 (and_2_out, not_1_out, not_2_out, not_3_out, not_4_out, flagfive[2], flagfive[0], flag_in[1], flag_in[0]);
  and and_3 (and_3_out, not_1_out, not_2_out, not_3_out, not_4_out, flagfive[2], flagfive[1], flag_in[1], flag_in[0]);
  and and_4 (and_4_out, not_1_out, not_2_out, outt[1], outt[0], flagfive[2], not_6_out, not_7_out, not_8_out, not_9_out);
  and and_5 (and_5_out, not_1_out, not_2_out, outt[1], outt[0], flagfive[2], flagfive[0], flag_in[1], flag_in[0]);
  and and_6 (and_6_out, not_1_out, not_2_out, outt[1], outt[0], flagfive[2], flagfive[1], flag_in[1], flag_in[0]);
  and and_7 (and_7_out, not_1_out, outt[2], not_3_out, outt[0], flagfive[2], not_6_out, not_7_out, not_8_out, not_9_out);
  and and_8 (and_8_out, not_1_out, outt[2], not_3_out, outt[0], flagfive[2], flagfive[0], flag_in[1], flag_in[0]);
  and and_9 (and_9_out, not_1_out, outt[2], not_3_out, outt[0], flagfive[2], flagfive[1], flag_in[1], flag_in[0]);
  and and_10 (and_10_out, not_1_out, outt[2], outt[1], not_4_out, flagfive[2], not_6_out, not_7_out, not_8_out, not_9_out);
  and and_11 (and_11_out, not_1_out, outt[2], outt[1], not_4_out, flagfive[2], flagfive[0], flag_in[1], flag_in[0]);
  and and_12 (and_12_out, not_1_out, outt[2], outt[1], not_4_out, flagfive[2], flagfive[1], flag_in[1], flag_in[0]);
  and and_13 (and_13_out, outt[3], not_2_out, not_3_out, outt[0], flagfive[2], not_6_out, not_7_out, not_8_out, not_9_out);
  and and_14 (and_14_out, outt[3], not_2_out, not_3_out, outt[0], flagfive[2], flagfive[0], flag_in[1], flag_in[0]);
  and and_15 (and_15_out, outt[3], not_2_out, not_3_out, outt[0], flagfive[2], flagfive[1], flag_in[1], flag_in[0]);
  and and_16 (and_16_out, outt[3], not_2_out, outt[1], not_4_out, flagfive[2], not_6_out, not_7_out, not_8_out, not_9_out);
  and and_17 (and_17_out, outt[3], not_2_out, outt[1], not_4_out, flagfive[2], flagfive[0], flag_in[1], flag_in[0]);
  and and_18 (and_18_out, outt[3], not_2_out, outt[1], not_4_out, flagfive[2], flagfive[1], flag_in[1], flag_in[0]);
  and and_19 (and_19_out, outt[3], outt[2], not_3_out, not_4_out, flagfive[2], not_6_out, not_7_out, not_8_out, not_9_out);
  and and_20 (and_20_out, outt[3], outt[2], not_3_out, not_4_out, flagfive[2], flagfive[0], flag_in[1], flag_in[0]);
  and and_21 (and_21_out, outt[3], outt[2], not_3_out, not_4_out, flagfive[2], flagfive[1], flag_in[1], flag_in[0]);
  and and_22 (and_22_out, outt[3], outt[2], outt[1], outt[0], flagfive[2], not_6_out, not_7_out, not_8_out, not_9_out);
  and and_23 (and_23_out, outt[3], outt[2], outt[1], outt[0], flagfive[2], flagfive[0], flag_in[1], flag_in[0]);
  and and_24 (and_24_out, outt[3], outt[2], outt[1], outt[0], flagfive[2], flagfive[1], flag_in[1], flag_in[0]);
  and and_25 (and_25_out, flagfive[2], not_8_out, flag_in[0]);
  and and_26 (and_26_out, flagfive[2], flag_in[1], not_9_out);
  and and_27 (flag_out[0], flagfive[2], not_9_out);
  and and_28 (and_28_out, flagfive[1], flagfive[0]);
  and and_29 (and_29_out, not_6_out, flagfive[0]);
  and and_30 (and_30_out, flagfive[1], not_7_out);
  and and_31 (fllagfive[0], not_5_out, not_7_out);
  or or_1 (flag_out[1], and_25_out, and_26_out);
  or or_2 (fllagfive[2], and_28_out, flagfive[2]);
  or or_3 (fllagfive[1], and_29_out, and_30_out);
  or or_4 (even, and_1_out, and_2_out, and_3_out, and_4_out, and_5_out, and_6_out, and_7_out, and_8_out, and_9_out, and_10_out, and_11_out, and_12_out, and_13_out, and_14_out, and_15_out, and_16_out, and_17_out, and_18_out, and_19_out, and_20_out, and_21_out, and_22_out, and_23_out, and_24_out);
endmodule
