// Logisim project FourBitParitygrader.circ as structural Verilog: 4 circuits, main circuit main
module main (
  input  StopOnMismatchIn,
  output [6:0] TestNumberOut,
  output IsEvenOut,
  output BitsOut,
  output ClkOut,
  output halt
);

  wire and_1_out, CorrectAnswer, not_1_out, StopTesting, StudentAnswerIsCorrect;
  wire [6:0] counter_1_q;

  Clock clock_1 (.out(ClkOut));
  InputGenerator inputgenerator_1 (
    .StopTestingIn(StopTesting), .ClkIn(ClkOut), .TestNumberOut(TestNumberOut), .BitsOut(BitsOut),
    .DoneTestingOut(halt));
  and and_1 (and_1_out, StudentAnswerIsCorrect, ~halt, ~StopTesting);  // AND_Gate
  not not_1 (not_1_out, StopTesting);
  // Probe on BitsOut
  // Probe on TestNumberOut
  // Probe on StudentAnswerIsCorrect
  // Probe on IsEvenOut
  Counter #(.max('h41), .ongoal("stay"), .width(7)) counter_1 (
    .up(and_1_out), .count(and_1_out), .clk(ClkOut), .Q(counter_1_q));  // open: clr, load, D, carry
  // Probe on IsEvenOut
  implementation implementation_1 (.EnableIn(not_1_out), .InputBitIn(BitsOut), .ClkIn(ClkOut), .IsEvenOut(IsEvenOut));
  // Probe on CorrectAnswer
  // Probe on counter_1_q
  // Probe on TestNumberOut
  // Probe on CorrectAnswer
  \checker  checker_1 (
    .TestNumberIn(TestNumberOut), .StudentAnswerIn(IsEvenOut), .StopOnMismatchIn(StopOnMismatchIn),
    .clkIn(ClkOut), .CorrectAnswerOut(CorrectAnswer), .StudentAnswerIsCorrectOut(StudentAnswerIsCorrect),
    .StopTestingOut(StopTesting));

  // Other names for the same wires on the sheet: Bits = BitsOut; Clk = ClkOut; IsEven = IsEvenOut; Stop = halt;
  //   StopOnMismatch = StopOnMismatchIn; TestNumber[6:0] = TestNumberOut

  // Notes on the sheet:
  //   SetStepOnMismatch to 1 to have the testing circuit stop on the first output that is incorrect
  //   Maximum Number Correct is 65
endmodule

module InputGenerator (
  input  StopTestingIn,
  input  ClkIn,
  output [6:0] TestNumberOut,
  output BitsOut,
  output DoneTestingOut
);

  wire not_1_out;

  not not_1 (not_1_out, StopTestingIn);
  Counter #(.max('h41), .ongoal("stay"), .width(7)) counter_1 (
    .up(1'b1), .count(not_1_out), .clk(ClkIn), .carry(DoneTestingOut), .Q(TestNumberOut));  // open: clr, load, D
  ROM #(.addrWidth(7), .dataWidth(1)) rom_1 (.addr(TestNumberOut));  // open: data

  // Other names for the same wires on the sheet: clk = ClkIn; done_testing = DoneTestingOut;
  //   StopTesting = StopTestingIn; TestNumber[6:0] = TestNumberOut

  // Notes on the sheet:
  //   contents of rom_1 (hex, n*v repeats v):
  //   7*0 1 0 0 1 0 0 0 1 1 0 1 0 0 0 1 0 1 0 1 1 0 0 4*1 0 0 0 1 0 0 1 1 0 1 0 1 0 4*1 0 0 1 1 0 4*1 0
  //   4*1
endmodule

module \checker  (
  input  [6:0] TestNumberIn,
  input  StudentAnswerIn,
  input  StopOnMismatchIn,
  input  clkIn,
  output CorrectAnswerOut,
  output StudentAnswerIsCorrectOut,
  output StopTestingOut
);

  Comparator #(.width(1)) comparator_1 (
    .a(StudentAnswerIn), .b(CorrectAnswerOut), .eq(StudentAnswerIsCorrectOut));  // open: gt, lt
  stop_testing_circ stop_testing_circ_1 (
    .StopOnIncorrectIn(StopOnMismatchIn), .AnswerIsCorrectIn(StudentAnswerIsCorrectOut), .ClkIn(clkIn),
    .StopTestingOut(StopTestingOut));
  ROM #(.addrWidth(7), .dataWidth(1)) rom_1 (.addr(TestNumberIn));  // open: data

  // Other names for the same wires on the sheet: clk = clkIn; CorrectAnswer = CorrectAnswerOut;
  //   StopOnMismatch = StopOnMismatchIn; StopTesting = StopTestingOut; StudentAnswer = StudentAnswerIn;
  //   StudentAnswerIsCorrect = StudentAnswerIsCorrectOut; TestNumber[6:0] = TestNumberIn

  // Notes on the sheet:
  //   contents of rom_1 (hex, n*v repeats v):
  //   4*0 1 11*0 1 7*0 1 0 0 0 1 11*0 1 0 0 0 1 7*0 1 11*0 1
endmodule

module stop_testing_circ (
  input  StopOnIncorrectIn,
  input  AnswerIsCorrectIn,
  input  ClkIn,
  output StopTestingOut
);

  wire SavedStopTesting, StopTesting;

  and and_1 (StopTesting, ~AnswerIsCorrectIn, StopOnIncorrectIn);  // AND_Gate
  Register #(.width(1)) register_1 (.D(StopTesting), .en(StopTesting), .clk(ClkIn), .Q(SavedStopTesting));  // open: clr
  or or_1 (StopTestingOut, StopTesting, SavedStopTesting);

  // Other names for the same wires on the sheet: AnswerIsCorrect = AnswerIsCorrectIn; clk = ClkIn;
  //   StopOnIncorrect = StopOnIncorrectIn
endmodule
