// Logisim project UpDownCounter.circ as structural Verilog: 2 circuits, main circuit implementation
module implementation (
  input  EnableIn,
  input  CountUpIn,
  input  CountDownIn,
  input  clkIn,
  output [2:0] Count
);

  wire [2:0] addminus_1_stateout;

  Register #(.width(3)) register_1 (.D(addminus_1_stateout), .en(EnableIn), .clk(clkIn), .Q(Count));  // open: clr
  addminus addminus_1 (
    .CountUpIn(CountUpIn), .CountDownIn(CountDownIn), .stateIn(Count), .stateout(addminus_1_stateout));

  // Other names for the same wires on the sheet: ans[2:0] = Count; clk = clkIn; CountDown = CountDownIn;
  //   CountUp = CountUpIn; Enable = EnableIn
endmodule

module addminus (
  input  CountUpIn,
  input  CountDownIn,
  input  [2:0] stateIn,
  output [2:0] stateout
);

  wire and_1_out, and_2_out, and_3_out, and_4_out, and_5_out, and_6_out, and_7_out, and_8_out, and_9_out,
       and_10_out, and_11_out, and_12_out, and_13_out, and_14_out, not_1_out, not_2_out, not_3_out, not_4_out;

  not not_1 (not_1_out, CountUpIn);
  not not_2 (not_2_out, CountDownIn);
  not not_3 (not_3_out, stateIn[1]);
  not not_4 (not_4_out, stateIn[0]);
  and and_1 (and_1_out, not_2_out, stateIn[2]);
  and and_2 (and_2_out, stateIn[2], stateIn[0]);
  and and_3 (and_3_out, stateIn[2], stateIn[1]);
  and and_4 (and_4_out, CountUpIn, stateIn[1], stateIn[0]);
  and and_5 (and_5_out, not_2_out, stateIn[1], not_4_out);
  and and_6 (and_6_out, not_1_out, stateIn[1], stateIn[0]);
  and and_7 (and_7_out, not_2_out, stateIn[2], stateIn[1]);
  and and_8 (and_8_out, CountDownIn, stateIn[2], not_3_out, not_4_out);
  and and_9 (and_9_out, CountUpIn, not_3_out, stateIn[0]);
  and and_10 (and_10_out, not_1_out, not_2_out, stateIn[0]);
  and and_11 (and_11_out, not_2_out, stateIn[2], stateIn[1], stateIn[0]);
  and and_12 (and_12_out, CountDownIn, stateIn[1], not_4_out);
  and and_13 (and_13_out, CountDownIn, stateIn[2], not_4_out);
  and and_14 (and_14_out, CountUpIn, not_4_out);
  or or_1 (stateout[2], and_1_out, and_2_out, and_3_out, and_4_out);
  or or_2 (stateout[1], and_5_out, and_6_out, and_7_out, and_8_out, and_9_out);
  or or_3 (stateout[0], and_10_out, and_11_out, and_12_out, and_13_out, and_14_out);
endmodule
