// Logisim project Vending.circ as structural Verilog: 3 circuits, main circuit implementation
module implementation (
  input  EnableIn,
  input  QuarterReceivedIn,
  input  DimeReceivedIn,
  input  NickelReceivedIn,
  input  ClkIn,
  output Give_Mechandise_Out,
  output Give_Dime_Out,
  output Give_Nickel_Out
);

  wire [5:0] register_1_q, state;

  adding adding_1 (
    .QuarterReceivedIn(QuarterReceivedIn), .DimeReceivedIn(DimeReceivedIn),
    .NickelReceivedIn(NickelReceivedIn), .a(register_1_q), .moneyout(state));
  // Probe on state
  // Probe on register_1_q
  outt outt_1 (
    .inn(state), .Give_Mechandise_Out(Give_Mechandise_Out), .Give_Dime_Out(Give_Dime_Out),
    .Give_Nickel_Out(Give_Nickel_Out));
  Register #(.width(6)) register_1 (.D(state), .en(EnableIn), .clk(ClkIn), .Q(register_1_q));  // open: clr
  // Probe on register_1_q

  // Other names for the same wires on the sheet: clk = ClkIn; DimeReceieved = DimeReceivedIn; Enable = EnableIn;
  //   Give_Dime = Give_Dime_Out; Give_Merchandise = Give_Mechandise_Out; Give_Nickel = Give_Nickel_Out;
  //   NickelReceieved = NickelReceivedIn; QuarterReceieved = QuarterReceivedIn
endmodule

module adding (
  input  QuarterReceivedIn,
  input  DimeReceivedIn,
  input  NickelReceivedIn,
  input  [5:0] a,
  output [5:0] moneyout
);

  wire and_1_out, and_2_out, and_3_out, and_4_out, and_5_out, and_6_out, and_7_out, and_8_out, and_9_out,
       and_10_out, and_11_out, and_12_out, and_13_out, and_14_out, and_15_out, and_16_out, and_17_out,
       and_18_out, and_19_out, and_20_out, and_21_out, and_22_out, and_23_out, and_24_out, and_25_out,
       and_26_out, and_27_out, and_28_out, and_29_out, and_30_out, and_31_out, and_32_out, and_33_out,
       and_34_out, and_35_out, and_36_out, and_37_out, and_38_out, and_39_out, and_40_out, and_41_out,
       and_42_out, and_43_out, and_44_out, and_45_out, and_46_out, and_47_out, and_48_out, and_49_out,
       and_50_out, and_51_out, and_52_out, and_53_out, and_54_out, and_55_out, and_56_out, and_57_out,
       and_58_out, and_59_out, and_60_out, and_61_out, and_62_out, and_63_out, and_64_out, and_65_out,
       and_66_out, and_67_out, and_68_out, and_69_out, and_70_out, and_71_out, and_72_out, and_73_out,
       and_74_out, and_75_out, and_76_out, and_77_out, and_78_out, and_79_out, and_80_out, and_81_out,
       and_82_out, and_83_out, and_84_out, and_85_out, and_86_out, and_87_out, and_88_out, not_1_out,
       not_2_out, not_3_out, not_4_out, not_5_out, not_6_out, not_7_out, not_8_out, not_9_out;

  not not_1 (not_1_out, QuarterReceivedIn);
  not not_2 (not_2_out, DimeReceivedIn);
  not not_3 (not_3_out, NickelReceivedIn);
  not not_4 (not_4_out, a[5]);
  not not_5 (not_5_out, a[4]);
  not not_6 (not_6_out, a[3]);
  not not_7 (not_7_out, a[2]);
  not not_8 (not_8_out, a[1]);
  not not_9 (not_9_out, a[0]);
  and and_1 (and_1_out, DimeReceivedIn, not_3_out, not_4_out, not_7_out, a[0]);
  and and_2 (and_2_out, QuarterReceivedIn, not_3_out, not_4_out, not_7_out, a[0]);
  and and_3 (and_3_out, QuarterReceivedIn, not_4_out, not_5_out, a[3]);
  and and_4 (and_4_out, QuarterReceivedIn, not_4_out, a[4], not_6_out);
  and and_5 (and_5_out, QuarterReceivedIn, not_4_out, a[4], not_7_out);
  and and_6 (and_6_out, QuarterReceivedIn, not_4_out, a[4], not_8_out);
  and and_7 (and_7_out, QuarterReceivedIn, NickelReceivedIn, a[3]);
  and and_8 (and_8_out, QuarterReceivedIn, NickelReceivedIn, a[4]);
  and and_9 (and_9_out, QuarterReceivedIn, DimeReceivedIn, not_3_out, not_7_out, a[0]);
  and and_10 (and_10_out, QuarterReceivedIn, DimeReceivedIn, a[3]);
  and and_11 (and_11_out, QuarterReceivedIn, DimeReceivedIn, a[4]);
  and and_12 (and_12_out, not_1_out, not_2_out, not_4_out, a[4], not_7_out);
  and and_13 (and_13_out, not_1_out, not_4_out, a[4], not_6_out);
  and and_14 (and_14_out, not_1_out, not_4_out, a[4], a[2], not_8_out);
  and and_15 (and_15_out, not_1_out, NickelReceivedIn, not_4_out, not_5_out, a[3], a[2]);
  and and_16 (and_16_out, DimeReceivedIn, not_3_out, not_4_out, not_5_out, a[1]);
  and and_17 (and_17_out, DimeReceivedIn, not_4_out, a[3], not_7_out, a[1]);
  and and_18 (and_18_out, not_1_out, DimeReceivedIn, not_4_out, not_5_out, a[3], a[2]);
  and and_19 (and_19_out, DimeReceivedIn, NickelReceivedIn, a[2], a[1]);
  and and_20 (and_20_out, not_1_out, DimeReceivedIn, NickelReceivedIn, a[3], a[2]);
  and and_21 (and_21_out, DimeReceivedIn, NickelReceivedIn, a[4]);
  and and_22 (and_22_out, DimeReceivedIn, NickelReceivedIn, a[5], a[1]);
  and and_23 (and_23_out, QuarterReceivedIn, not_5_out, not_6_out);
  and and_24 (and_24_out, QuarterReceivedIn, not_7_out, not_8_out);
  and and_25 (and_25_out, QuarterReceivedIn, a[4], a[3], a[2], a[1]);
  and and_26 (and_26_out, QuarterReceivedIn, not_2_out, not_3_out, a[5]);
  and and_27 (and_27_out, QuarterReceivedIn, NickelReceivedIn, a[4]);
  and and_28 (and_28_out, QuarterReceivedIn, DimeReceivedIn, a[1]);
  and and_29 (and_29_out, not_1_out, not_2_out, not_4_out, a[3], not_7_out);
  and and_30 (and_30_out, not_3_out, not_4_out, not_5_out, a[3], a[2]);
  and and_31 (and_31_out, not_3_out, not_4_out, a[3], a[2], not_8_out);
  and and_32 (and_32_out, NickelReceivedIn, not_4_out, not_6_out, a[2]);
  and and_33 (and_33_out, not_1_out, DimeReceivedIn, not_4_out, not_5_out, not_6_out);
  and and_34 (and_34_out, DimeReceivedIn, not_3_out, not_6_out);
  and and_35 (and_35_out, DimeReceivedIn, not_3_out, a[2]);
  and and_36 (and_36_out, DimeReceivedIn, not_6_out, a[2]);
  and and_37 (and_37_out, not_1_out, DimeReceivedIn, not_3_out, a[5]);
  and and_38 (and_38_out, DimeReceivedIn, NickelReceivedIn, a[3], not_7_out);
  and and_39 (and_39_out, QuarterReceivedIn, not_2_out, not_4_out, not_5_out, not_6_out, not_8_out, not_9_out);
  and and_40 (and_40_out, QuarterReceivedIn, not_3_out, not_6_out);
  and and_41 (and_41_out, QuarterReceivedIn, not_3_out, a[2]);
  and and_42 (and_42_out, QuarterReceivedIn, not_6_out, a[2]);
  and and_43 (and_43_out, QuarterReceivedIn, not_2_out, not_3_out, a[5]);
  and and_44 (and_44_out, QuarterReceivedIn, NickelReceivedIn, a[3], not_7_out);
  and and_45 (and_45_out, not_3_out, not_4_out, not_6_out, a[2]);
  and and_46 (and_46_out, not_1_out, not_2_out, not_4_out, not_5_out, a[3], a[2]);
  and and_47 (and_47_out, not_1_out, not_2_out, not_4_out, a[3], a[2], not_8_out);
  and and_48 (and_48_out, not_1_out, not_2_out, NickelReceivedIn, not_7_out);
  and and_49 (and_49_out, NickelReceivedIn, a[3], a[0]);
  and and_50 (and_50_out, NickelReceivedIn, a[4], not_7_out);
  and and_51 (and_51_out, not_1_out, not_2_out, NickelReceivedIn, a[5]);
  and and_52 (and_52_out, NickelReceivedIn, a[5], not_7_out);
  and and_53 (and_53_out, not_1_out, DimeReceivedIn, not_3_out, not_4_out, not_7_out, a[1]);
  and and_54 (and_54_out, DimeReceivedIn, NickelReceivedIn, a[3]);
  and and_55 (and_55_out, QuarterReceivedIn, NickelReceivedIn, not_7_out, a[0]);
  and and_56 (and_56_out, QuarterReceivedIn, NickelReceivedIn, not_7_out, a[1]);
  and and_57 (and_57_out, QuarterReceivedIn, NickelReceivedIn, a[3]);
  and and_58 (and_58_out, QuarterReceivedIn, DimeReceivedIn, not_3_out, not_6_out, a[2]);
  and and_59 (and_59_out, QuarterReceivedIn, DimeReceivedIn, NickelReceivedIn, not_7_out);
  and and_60 (and_60_out, not_1_out, not_2_out, not_3_out, not_4_out, not_5_out, a[1]);
  and and_61 (and_61_out, not_1_out, not_3_out, not_4_out, not_6_out, a[1]);
  and and_62 (and_62_out, not_2_out, not_4_out, not_7_out, a[1]);
  and and_63 (and_63_out, NickelReceivedIn, not_4_out, not_8_out, a[0]);
  and and_64 (and_64_out, DimeReceivedIn, not_6_out);
  and and_65 (and_65_out, DimeReceivedIn, not_8_out, a[0]);
  and and_66 (and_66_out, not_1_out, DimeReceivedIn, not_3_out, a[4], a[2], a[1]);
  and and_67 (and_67_out, not_1_out, DimeReceivedIn, not_3_out, a[5]);
  and and_68 (and_68_out, QuarterReceivedIn, not_4_out, not_8_out, a[0]);
  and and_69 (and_69_out, QuarterReceivedIn, NickelReceivedIn, not_8_out, a[0]);
  and and_70 (and_70_out, QuarterReceivedIn, not_2_out, NickelReceivedIn, not_7_out, a[1]);
  and and_71 (and_71_out, not_1_out, not_3_out, not_4_out, not_5_out, a[0]);
  and and_72 (and_72_out, not_1_out, not_3_out, not_4_out, not_6_out, a[0]);
  and and_73 (and_73_out, not_1_out, not_3_out, not_4_out, not_7_out, a[0]);
  and and_74 (and_74_out, not_1_out, not_3_out, not_4_out, not_8_out, a[0]);
  and and_75 (and_75_out, not_2_out, NickelReceivedIn, not_5_out, not_9_out);
  and and_76 (and_76_out, not_2_out, NickelReceivedIn, not_6_out, not_9_out);
  and and_77 (and_77_out, not_2_out, NickelReceivedIn, not_7_out, not_9_out);
  and and_78 (and_78_out, not_2_out, NickelReceivedIn, not_8_out, not_9_out);
  and and_79 (and_79_out, not_1_out, NickelReceivedIn, a[4], a[3], a[2], a[1], a[0]);
  and and_80 (and_80_out, not_2_out, NickelReceivedIn, a[5], not_9_out);
  and and_81 (and_81_out, not_1_out, NickelReceivedIn, a[5], a[0]);
  and and_82 (and_82_out, DimeReceivedIn, NickelReceivedIn, a[2], a[1], a[0]);
  and and_83 (and_83_out, DimeReceivedIn, NickelReceivedIn, a[3], a[0]);
  and and_84 (and_84_out, DimeReceivedIn, NickelReceivedIn, a[4], a[0]);
  and and_85 (and_85_out, QuarterReceivedIn, not_2_out, not_9_out);
  and and_86 (and_86_out, QuarterReceivedIn, not_3_out, a[4], a[3], a[2], a[1], a[0]);
  and and_87 (and_87_out, QuarterReceivedIn, not_2_out, not_3_out, a[5]);
  and and_88 (and_88_out, QuarterReceivedIn, DimeReceivedIn, a[0]);
  or or_1 (moneyout[5], and_1_out, and_2_out, and_3_out, and_4_out, and_5_out, and_6_out, and_7_out, and_8_out, and_9_out, and_10_out, and_11_out);
  or or_2 (moneyout[1], and_60_out, and_61_out, and_62_out, and_63_out, and_64_out, and_65_out, and_66_out, and_67_out, and_68_out, and_69_out, and_70_out);
  or or_3 (moneyout[4], and_12_out, and_13_out, and_14_out, and_15_out, and_16_out, and_17_out, and_18_out, and_19_out, and_20_out, and_21_out, and_22_out, and_23_out, and_24_out, and_25_out, and_26_out, and_27_out, and_28_out);
  or or_4 (moneyout[3], and_29_out, and_30_out, and_31_out, and_32_out, and_33_out, and_34_out, and_35_out, and_36_out, and_37_out, and_38_out, and_39_out, and_40_out, and_41_out, and_42_out, and_43_out, and_44_out);
  or or_5 (moneyout[2], and_45_out, and_46_out, and_47_out, and_48_out, and_49_out, and_50_out, and_51_out, and_52_out, and_53_out, and_54_out, and_55_out, and_56_out, and_57_out, and_58_out, and_59_out);
  or or_6 (moneyout[0], and_71_out, and_72_out, and_73_out, and_74_out, and_75_out, and_76_out, and_77_out, and_78_out, and_79_out, and_80_out, and_81_out, and_82_out, and_83_out, and_84_out, and_85_out, and_86_out, and_87_out, and_88_out);
endmodule

module outt (
  input  [5:0] inn,
  output Give_Mechandise_Out,
  output Give_Dime_Out,
  output Give_Nickel_Out
);

  wire and_1_out, and_2_out, and_3_out, and_4_out, and_5_out, not_1_out, not_2_out, not_3_out;

  not not_1 (not_1_out, inn[3]);
  not not_2 (not_2_out, inn[1]);
  not not_3 (not_3_out, inn[0]);
  and and_1 (and_1_out, inn[4], inn[3], inn[2], inn[1]);
  or or_1 (Give_Mechandise_Out, and_1_out, inn[5]);
  and and_2 (and_2_out, inn[5], not_2_out);
  or or_2 (Give_Dime_Out, and_2_out, and_3_out);
  and and_3 (and_3_out, inn[5], not_3_out);
  and and_4 (and_4_out, inn[5], not_1_out);
  or or_3 (Give_Nickel_Out, and_4_out, and_5_out);
  and and_5 (and_5_out, inn[5], inn[2]);
endmodule
