// Logisim project Vendinggrader.circ as structural Verilog: 4 circuits, main circuit main
module main (
  input  StopOnMismatchIn,
  output [8:0] TestNumberOut,
  output GiveMerchandiseOut,
  output GiveDimeOut,
  output GiveNickelOut,
  output QuarterReceivedOut,
  output DimeReceivedOut,
  output NickelReceivedOut,
  output ClkOut,
  output halt
);

  wire and_1_out, Correct_Give_Dime, Correct_Give_Merchandise, Correct_Give_Nickel, not_1_out, StopTesting,
       StudentAnswerIsCorrect;
  wire [8:0] counter_1_q;

  Clock clock_1 (.out(ClkOut));
  InputGenerator inputgenerator_1 (
    .StopTestingIn(StopTesting), .ClkIn(ClkOut), .TestNumberOut(TestNumberOut),
    .QuarterReceivedOut(QuarterReceivedOut), .DimeReceivedOut(DimeReceivedOut),
    .NickelReceivedOut(NickelReceivedOut), .DoneTestingOut(halt));
  and and_1 (and_1_out, StudentAnswerIsCorrect, ~halt, ~StopTesting);  // AND_Gate
  // Probe on Correct_Give_Merchandise
  // Probe on Correct_Give_Dime
  // Probe on Correct_Give_Nickel
  Counter #(.max('h162), .ongoal("stay"), .width(9)) counter_1 (
    .up(and_1_out), .count(and_1_out), .clk(ClkOut), .Q(counter_1_q));  // open: clr, load, D, carry
  not not_1 (not_1_out, StopTesting);
  // Probe on TestNumberOut
  // Probe on StudentAnswerIsCorrect
  implementation implementation_1 (
    .EnableIn(not_1_out), .QuarterReceivedIn(QuarterReceivedOut), .DimeReceivedIn(DimeReceivedOut),
    .NickelReceivedIn(NickelReceivedOut), .ClkIn(ClkOut), .Give_Mechandise_Out(GiveMerchandiseOut),
    .Give_Dime_Out(GiveDimeOut), .Give_Nickel_Out(GiveNickelOut));
  // Probe on GiveMerchandiseOut
  // Probe on GiveDimeOut
  // Probe on GiveNickelOut
  // Probe on counter_1_q
  \checker  checker_1 (
    .TestNumberIn(TestNumberOut), .StudentAnswerIn({GiveMerchandiseOut, GiveDimeOut, GiveNickelOut}),
    .StopOnMismatchIn(StopOnMismatchIn), .clkIn(ClkOut), .CorrectGiveMerchandise(Correct_Give_Merchandise),
    .CorrectGiveDime(Correct_Give_Dime), .CorrectGiveNickel(Correct_Give_Nickel),
    .StudentAnswerIsCorrectOut(StudentAnswerIsCorrect), .StopTestingOut(StopTesting));

  // Other names for the same wires on the sheet: Give_Nickel = GiveNickelOut; Give_Dime = GiveDimeOut;
  //   Give_Merchandise = GiveMerchandiseOut; Clk = ClkOut; DimeReceieved = DimeReceivedOut;
  //   NickelReceieved = NickelReceivedOut; QuarterReceieved = QuarterReceivedOut; Stop = halt;
  //   StopOnMismatch = StopOnMismatchIn; TestNumber[8:0] = TestNumberOut

  // Notes on the sheet:
  //   SetStepOnMismatch to 1 to have the testing circuit stop on the first output that is incorrect
  //   Maximum Number of Points is 354
endmodule

module InputGenerator (
  input  StopTestingIn,
  input  ClkIn,
  output [8:0] TestNumberOut,
  output QuarterReceivedOut,
  output DimeReceivedOut,
  output NickelReceivedOut,
  output DoneTestingOut
);

  wire not_1_out;

  not not_1 (not_1_out, StopTestingIn);
  Counter #(.max('h162), .ongoal("stay"), .width(9)) counter_1 (
    .up(1'b1), .count(not_1_out), .clk(ClkIn), .carry(DoneTestingOut), .Q(TestNumberOut));  // open: clr, load, D
  ROM #(.addrWidth(9), .dataWidth(3)) rom_1 (
    .addr(TestNumberOut), .data({QuarterReceivedOut, DimeReceivedOut, NickelReceivedOut}));

  // Other names for the same wires on the sheet: clk = ClkIn; done_testing = DoneTestingOut;
  //   StopTesting = StopTestingIn; TestNumber[8:0] = TestNumberOut

  // Notes on the sheet:
  //   contents of rom_1 (hex, n*v repeats v):
  //   1 0 1 0 1 0 1 0 1 0 1 0 1 0 1 0 1 0 1 0 1 0 2 0 1 0 1 0 1 0 1 0 1 0 4 0 1 0 1 0 1 0 1 0 2 0 1 0 1 0
  //   1 0 1 0 4 0 1 0 1 0 1 0 1 0 2 0 1 0 1 0 1 0 2 0 2 0 1 0 1 0 1 0 2 0 4 0 1 0 1 0 1 0 4 0 1 0 1 0 1 0
  //   1 0 2 0 1 0 1 0 1 0 2 0 2 0 1 0 1 0 1 0 2 0 4 0 1 0 1 0 2 0 2 0 1 0 1 0 2 0 4 0 1 0 1 0 4 0 1 0 1 0
  //   1 0 1 0 2 0 1 0 1 0 1 0 2 0 2 0 1 0 1 0 1 0 2 0 4 0 1 0 1 0 2 0 2 0 1 0 1 0 2 0 4 0 1 0 1 0 2 0 2 0
  //   1 0 2 0 2 0 2 0 1 0 2 0 2 0 4 0 1 0 2 0 4 0 1 0 4 0 1 0 1 0 1 0 1 0 2 0 1 0 1 0 1 0 2 0 2 0 1 0 1 0
  //   1 0 2 0 4 0 1 0 1 0 2 0 2 0 1 0 1 0 2 0 4 0 1 0 1 0 2 0 2 0 1 0 2 0 2 0 2 0 1 0 2 0 2 0 4 0 1 0 2 0
  //   4 0 1 0 1 0 2 0 2 0 1 0 2 0 2 0 2 0 1 0 2 0 2 0 4 0 2 0 2 0 2 0 2 0 2 0 4 0 2 0 4 0 1 0 4 0 2 0 4 0
  //   4 0 4
endmodule

module \checker  (
  input  [8:0] TestNumberIn,
  input  [2:0] StudentAnswerIn,
  input  StopOnMismatchIn,
  input  clkIn,
  output CorrectGiveMerchandise,
  output CorrectGiveDime,
  output CorrectGiveNickel,
  output StudentAnswerIsCorrectOut,
  output StopTestingOut
);

  Comparator #(.width(3)) comparator_1 (
    .a(StudentAnswerIn), .b({CorrectGiveMerchandise, CorrectGiveDime, CorrectGiveNickel}),
    .eq(StudentAnswerIsCorrectOut));  // open: gt, lt
  stop_testing_circ stop_testing_circ_1 (
    .StopOnIncorrectIn(StopOnMismatchIn), .AnswerIsCorrectIn(StudentAnswerIsCorrectOut), .ClkIn(clkIn),
    .StopTestingOut(StopTestingOut));
  ROM #(.addrWidth(9), .dataWidth(3)) rom_1 (
    .addr(TestNumberIn), .data({CorrectGiveMerchandise, CorrectGiveDime, CorrectGiveNickel}));

  // Other names for the same wires on the sheet: clk = clkIn;
  //   CorrectAnswer[2:0] = {CorrectGiveMerchandise, CorrectGiveDime, CorrectGiveNickel};
  //   StopOnMismatch = StopOnMismatchIn; StopTesting = StopTestingOut; StudentAnswer[2:0] = StudentAnswerIn;
  //   StudentAnswerIsCorrect = StudentAnswerIsCorrectOut; TestNumber[8:0] = TestNumberIn

  // Notes on the sheet:
  //   contents of rom_1 (hex, n*v repeats v):
  //   10*0 4 11*0 5 11*0 7 9*0 4 9*0 7 9*0 4 9*0 5 9*0 7 7*0 6 9*0 4 9*0 5 9*0 7 7*0 4 7*0 7 5*0 5 9*0 4
  //   9*0 5 9*0 7 7*0 4 7*0 7 7*0 4 7*0 5 7*0 7 5*0 6 0 0 0 4 9*0 4 9*0 5 9*0 7 7*0 4 7*0 7 7*0 4 7*0 5
  //   7*0 7 5*0 6 7*0 4 7*0 5 7*0 7 5*0 4 5*0 7 0 0 0 5 0 0 0 4 0 0 0 5 0 0 0 7
endmodule

module stop_testing_circ (
  input  StopOnIncorrectIn,
  input  AnswerIsCorrectIn,
  input  ClkIn,
  output StopTestingOut
);

  wire SavedStopTesting, StopTesting;

  and and_1 (StopTesting, ~AnswerIsCorrectIn, StopOnIncorrectIn);  // AND_Gate
  Register #(.width(1)) register_1 (.D(StopTesting), .en(StopTesting), .clk(ClkIn), .Q(SavedStopTesting));  // open: clr
  or or_1 (StopTestingOut, StopTesting, SavedStopTesting);

  // Other names for the same wires on the sheet: AnswerIsCorrect = AnswerIsCorrectIn; clk = ClkIn;
  //   StopOnIncorrect = StopOnIncorrectIn
endmodule
