// Logisim project CPU.circ as structural Verilog: 8 circuits, main circuit implementation
module implementation (
  input  [15:0] Instruction_In,
  input  ClkIn,
  output [4:0] Instruction_Address_Out,
  output [3:0] Reg0_Out,
  output [3:0] Reg1_Out,
  output [3:0] Reg2_Out,
  output [3:0] Reg3_Out,
  output [3:0] Reg4_Out,
  output [3:0] Reg5_Out,
  output [3:0] Reg6_Out,
  output [3:0] Reg7_Out,
  output [3:0] Reg8_Out,
  output [3:0] Reg9_Out,
  output [3:0] Reg10_Out,
  output [3:0] Reg11_Out,
  output [3:0] Reg12_Out,
  output [3:0] Reg13_Out,
  output [3:0] Reg14_Out,
  output [3:0] Reg15_Out
);

  wire ChangeTrue, ItypeTure, StopTrue;
  wire [3:0] A_Value, AluResult, B_Value, multiplexer_1_out;
  wire [4:0] add_1_outt;

  Register #(.width(5)) PC (.D(add_1_outt), .en(StopTrue), .clk(ClkIn), .Q(Instruction_Address_Out));  // open: clr
  add add_1 (.in_1(Instruction_Address_Out), .outt(add_1_outt));
  RegFile regfile_1 (
    .A_Sel_In(Instruction_In[7:4]), .B_Sel_In(Instruction_In[3:0]), .C_Sel_In(Instruction_In[11:8]),
    .Data_In(AluResult), .Reg_Write_In(ChangeTrue), .clk_in(ClkIn), .A_Out(A_Value), .B_Out(B_Value),
    .Reg0_Out(Reg0_Out), .Reg1_Out(Reg1_Out), .Reg2_Out(Reg2_Out), .Reg3_Out(Reg3_Out), .Reg4_Out(Reg4_Out),
    .Reg5_Out(Reg5_Out), .Reg6_Out(Reg6_Out), .Reg7_Out(Reg7_Out), .Reg8_Out(Reg8_Out), .Reg9_Out(Reg9_Out),
    .Reg10_Out(Reg10_Out), .Reg11_Out(Reg11_Out), .Reg12_Out(Reg12_Out), .Reg13_Out(Reg13_Out),
    .Reg14_Out(Reg14_Out), .Reg15_Out(Reg15_Out));
  IsItype isitype_1 (.opselect(Instruction_In[15:12]), .ItypeTrue(ItypeTure));
  Multiplexer #(.enable("false"), .width(4)) multiplexer_1 (
    .in0(B_Value), .in1(Instruction_In[3:0]), .out(multiplexer_1_out), .sel(ItypeTure));
  IsStop isstop_1 (.a(Instruction_In[15:12]), .x(StopTrue));
  IsNochange isnochange_1 (.a(Instruction_In[15:12]), .x(ChangeTrue));
  ALU alu_1 (.OpSelect(Instruction_In[15:12]), .A(A_Value), .B(multiplexer_1_out), .Result(AluResult));

  // Other names for the same wires on the sheet: Clk = ClkIn; Immediate[3:0] = Instruction_In[3:0];
  //   Instruction[15:0] = Instruction_In; Rb[3:0] = Instruction_In[3:0]; Ra[3:0] = Instruction_In[7:4];
  //   Rc[3:0] = Instruction_In[11:8]; OpCode[3:0] = Instruction_In[15:12];
  //   Instruction_Address[4:0] = Instruction_Address_Out; Reg0[3:0] = Reg0_Out; Reg1[3:0] = Reg1_Out;
  //   Reg2[3:0] = Reg2_Out; Reg3[3:0] = Reg3_Out; Reg4[3:0] = Reg4_Out; Reg5[3:0] = Reg5_Out; Reg6[3:0] = Reg6_Out;
  //   Reg7[3:0] = Reg7_Out; Reg8[3:0] = Reg8_Out; Reg9[3:0] = Reg9_Out; Reg10[3:0] = Reg10_Out;
  //   Reg11[3:0] = Reg11_Out; Reg12[3:0] = Reg12_Out; Reg13[3:0] = Reg13_Out; Reg14[3:0] = Reg14_Out;
  //   Reg15[3:0] = Reg15_Out
endmodule

module RegFile (
  input  [3:0] A_Sel_In,
  input  [3:0] B_Sel_In,
  input  [3:0] C_Sel_In,
  input  [3:0] Data_In,
  input  Reg_Write_In,
  input  clk_in,
  output [3:0] A_Out,
  output [3:0] B_Out,
  output [3:0] Reg0_Out,
  output [3:0] Reg1_Out,
  output [3:0] Reg2_Out,
  output [3:0] Reg3_Out,
  output [3:0] Reg4_Out,
  output [3:0] Reg5_Out,
  output [3:0] Reg6_Out,
  output [3:0] Reg7_Out,
  output [3:0] Reg8_Out,
  output [3:0] Reg9_Out,
  output [3:0] Reg10_Out,
  output [3:0] Reg11_Out,
  output [3:0] Reg12_Out,
  output [3:0] Reg13_Out,
  output [3:0] Reg14_Out,
  output [3:0] Reg15_Out
);

  wire Reg_Write0, Reg_Write1, Reg_Write2, Reg_Write3, Reg_Write4, Reg_Write5, Reg_Write6, Reg_Write7,
       Reg_Write8, Reg_Write9, Reg_Write10, Reg_Write11, Reg_Write12, Reg_Write13, Reg_Write14, Reg_Write15;

  Demultiplexer #(.enable("false"), .select(4)) demultiplexer_1 (
    .out0(Reg_Write0), .out1(Reg_Write1), .out2(Reg_Write2), .out3(Reg_Write3), .out4(Reg_Write4),
    .out5(Reg_Write5), .out6(Reg_Write6), .out7(Reg_Write7), .out8(Reg_Write8), .out9(Reg_Write9),
    .out10(Reg_Write10), .out11(Reg_Write11), .out12(Reg_Write12), .out13(Reg_Write13), .out14(Reg_Write14),
    .out15(Reg_Write15), .in(Reg_Write_In), .sel(C_Sel_In));
  Register #(.width(4)) register_1 (.D(Data_In), .en(Reg_Write0), .clk(clk_in), .Q(Reg0_Out));  // open: clr
  Register #(.width(4)) register_2 (.D(Data_In), .en(Reg_Write4), .clk(clk_in), .Q(Reg4_Out));  // open: clr
  Register #(.width(4)) register_3 (.D(Data_In), .en(Reg_Write8), .clk(clk_in), .Q(Reg8_Out));  // open: clr
  Register #(.width(4)) register_4 (.D(Data_In), .en(Reg_Write12), .clk(clk_in), .Q(Reg12_Out));  // open: clr
  Register #(.width(4)) register_5 (.D(Data_In), .en(Reg_Write1), .clk(clk_in), .Q(Reg1_Out));  // open: clr
  Register #(.width(4)) register_6 (.D(Data_In), .en(Reg_Write5), .clk(clk_in), .Q(Reg5_Out));  // open: clr
  Register #(.width(4)) register_7 (.D(Data_In), .en(Reg_Write9), .clk(clk_in), .Q(Reg9_Out));  // open: clr
  Register #(.width(4)) register_8 (.D(Data_In), .en(Reg_Write13), .clk(clk_in), .Q(Reg13_Out));  // open: clr
  Register #(.width(4)) register_9 (.D(Data_In), .en(Reg_Write2), .clk(clk_in), .Q(Reg2_Out));  // open: clr
  Register #(.width(4)) register_10 (.D(Data_In), .en(Reg_Write6), .clk(clk_in), .Q(Reg6_Out));  // open: clr
  Register #(.width(4)) register_11 (.D(Data_In), .en(Reg_Write10), .clk(clk_in), .Q(Reg10_Out));  // open: clr
  Register #(.width(4)) register_12 (.D(Data_In), .en(Reg_Write14), .clk(clk_in), .Q(Reg14_Out));  // open: clr
  Register #(.width(4)) register_13 (.D(Data_In), .en(Reg_Write3), .clk(clk_in), .Q(Reg3_Out));  // open: clr
  Register #(.width(4)) register_14 (.D(Data_In), .en(Reg_Write7), .clk(clk_in), .Q(Reg7_Out));  // open: clr
  Register #(.width(4)) register_15 (.D(Data_In), .en(Reg_Write11), .clk(clk_in), .Q(Reg11_Out));  // open: clr
  Register #(.width(4)) register_16 (.D(Data_In), .en(Reg_Write15), .clk(clk_in), .Q(Reg15_Out));  // open: clr
  Multiplexer #(.enable("false"), .select(4), .width(4)) multiplexer_1 (
    .in0(Reg0_Out), .in1(Reg1_Out), .in2(Reg2_Out), .in3(Reg3_Out), .in4(Reg4_Out), .in5(Reg5_Out),
    .in6(Reg6_Out), .in7(Reg7_Out), .in8(Reg8_Out), .in9(Reg9_Out), .in10(Reg10_Out), .in11(Reg11_Out),
    .in12(Reg12_Out), .in13(Reg13_Out), .in14(Reg14_Out), .in15(Reg15_Out), .out(A_Out), .sel(A_Sel_In));
  Multiplexer #(.enable("false"), .select(4), .width(4)) multiplexer_2 (
    .in0(Reg0_Out), .in1(Reg1_Out), .in2(Reg2_Out), .in3(Reg3_Out), .in4(Reg4_Out), .in5(Reg5_Out),
    .in6(Reg6_Out), .in7(Reg7_Out), .in8(Reg8_Out), .in9(Reg9_Out), .in10(Reg10_Out), .in11(Reg11_Out),
    .in12(Reg12_Out), .in13(Reg13_Out), .in14(Reg14_Out), .in15(Reg15_Out), .out(B_Out), .sel(B_Sel_In));

  // Other names for the same wires on the sheet: A[3:0] = A_Out; A_Sel[3:0] = A_Sel_In; B[3:0] = B_Out;
  //   B_Sel[3:0] = B_Sel_In; C_Sel[3:0] = C_Sel_In; clk = clk_in; Data[3:0] = Data_In; Reg0[3:0] = Reg0_Out;
  //   Reg1[3:0] = Reg1_Out; Reg2[3:0] = Reg2_Out; Reg3[3:0] = Reg3_Out; Reg4[3:0] = Reg4_Out; Reg5[3:0] = Reg5_Out;
  //   Reg6[3:0] = Reg6_Out; Reg7[3:0] = Reg7_Out; Reg8[3:0] = Reg8_Out; Reg9[3:0] = Reg9_Out; Reg10[3:0] = Reg10_Out;
  //   Reg11[3:0] = Reg11_Out; Reg12[3:0] = Reg12_Out; Reg13[3:0] = Reg13_Out; Reg14[3:0] = Reg14_Out;
  //   Reg15[3:0] = Reg15_Out; Reg_Write = Reg_Write_In
endmodule

module ALU (
  input  [3:0] OpSelect,
  input  [3:0] A,
  input  [3:0] B,
  output [3:0] Result
);

  wire [3:0] adder_1_out, adder_2_out, and_1_out, chooose, not_1_out, not_2_out, or_1_out, subtractor_1_out,
       xor_1_out;

  assign and_1_out = A & B;  // AND_Gate and_1, 4 bits wide
  assign or_1_out = A | B;  // OR_Gate or_1, 4 bits wide
  assign xor_1_out = A ^ B;  // XOR_Gate xor_1, 4 bits wide
  assign not_1_out = ~A;  // NOT_Gate not_1, 4 bits wide
  assign not_2_out = ~A;  // NOT_Gate not_2, 4 bits wide
  Adder #(.width(4)) adder_1 (.a(not_2_out), .b(4'b0001), .out(adder_1_out));  // open: cin, cout
  Adder #(.width(4)) adder_2 (.a(A), .b(B), .out(adder_2_out));  // open: cin, cout
  Subtractor #(.width(4)) subtractor_1 (.a(A), .b(B), .out(subtractor_1_out));  // open: bin, bout
  // Probe on B
  chooseMUX choosemux_1 (.inpuut(OpSelect), .ouut(chooose));
  // Probe on Result
  Multiplexer #(.enable("false"), .select(4), .width(4)) multiplexer_1 (
    .in0(A), .in1(B), .in2(and_1_out), .in3(or_1_out), .in4(xor_1_out), .in5(not_1_out), .in6(adder_1_out),
    .in7(adder_2_out), .in8(subtractor_1_out), .out(Result), .sel(chooose));  // open: in9, in10, in11, in12, in13, in14, in15

  // Other names for the same wires on the sheet: resultt[3:0] = Result
endmodule

module IsItype (
  input  [3:0] opselect,
  output ItypeTrue
);

  wire and_1_out, and_2_out, and_3_out, not_1_out, not_2_out, not_3_out, not_4_out;

  not not_1 (not_1_out, opselect[3]);
  not not_2 (not_2_out, opselect[2]);
  not not_3 (not_3_out, opselect[1]);
  not not_4 (not_4_out, opselect[0]);
  and and_1 (and_1_out, not_1_out, not_2_out, opselect[1], not_4_out);
  and and_2 (and_2_out, opselect[2], opselect[0]);
  and and_3 (and_3_out, opselect[3], not_3_out, opselect[0]);
  or or_1 (ItypeTrue, and_1_out, and_2_out, and_3_out);
endmodule

module chooseMUX (
  input  [3:0] inpuut,
  output [3:0] ouut
);

  wire and_2_out, and_3_out, and_4_out, and_5_out, and_6_out, and_7_out, and_8_out, and_9_out, not_1_out,
       not_2_out, not_3_out, not_4_out;

  not not_1 (not_1_out, inpuut[3]);
  not not_2 (not_2_out, inpuut[2]);
  not not_3 (not_3_out, inpuut[1]);
  not not_4 (not_4_out, inpuut[0]);
  and and_1 (ouut[3], inpuut[3], inpuut[2], inpuut[1]);
  and and_2 (and_2_out, inpuut[3], not_2_out);
  and and_3 (and_3_out, inpuut[3], not_3_out);
  and and_4 (and_4_out, not_1_out, inpuut[2]);
  and and_5 (and_5_out, inpuut[2], not_3_out);
  and and_6 (and_6_out, inpuut[3], not_2_out, inpuut[1], inpuut[0]);
  and and_7 (and_7_out, not_2_out, inpuut[1], not_4_out);
  and and_8 (and_8_out, not_1_out, inpuut[2], inpuut[1]);
  and and_9 (and_9_out, inpuut[3], inpuut[2], not_3_out);
  or or_1 (ouut[2], and_2_out, and_3_out);
  or or_2 (ouut[1], and_4_out, and_5_out, and_6_out);
  or or_3 (ouut[0], and_7_out, and_8_out, and_9_out);
endmodule

module add (
  input  [4:0] in_1,
  output [4:0] outt
);

  Adder #(.width(5)) adder_1 (.a(in_1), .b(5'b00001), .out(outt));  // open: cin, cout

  // Other names for the same wires on the sheet: inss[4:0] = in_1
endmodule

module IsStop (
  input  [3:0] a,
  output x
);

  or or_1 (x, a[0], a[1], a[2], a[3]);
endmodule

module IsNochange (
  input  [3:0] a,
  output x
);

  or or_1 (x, a[1], a[2], a[3]);
endmodule
