// Logisim project MipsSingleCylceSpring2023.circ as structural Verilog: 4 circuits, main circuit MipsCPU
module MipsCPU (
  input  Clkin,
  input  [31:0] InstrIn,
  input  [31:0] DataValueFromMemoryIn,
  output [31:0] InstrAddressOut,
  output [31:0] MemoryAddress,
  output [31:0] DataToWrite,
  output WriteToMemoryOut
);

  wire AluControl, and_1_out, IsBranch, IsIType, IsJumpInstr, IsZero, MemoryRead, RegWrite;
  wire [4:0] multiplexer_3_out;
  wire [27:0] PCPlus4;
  wire [31:0] adder_2_out, AValue, multiplexer_1_out, multiplexer_2_out, multiplexer_4_out,
       multiplexer_5_out, SignExtendedImmediate;
  wire [31:28] JumpAddress;

  Adder #(.width(32)) adder_1 (.a(InstrAddressOut), .b(32'h4), .out({JumpAddress, PCPlus4}));  // open: cin, cout
  Adder #(.width(32)) adder_2 (
    .a({JumpAddress, PCPlus4}), .b(SignExtendedImmediate), .out(adder_2_out));  // open: cin, cout
  Multiplexer #(.enable("false"), .width(32)) multiplexer_1 (
    .in0({JumpAddress, PCPlus4}), .in1({JumpAddress, InstrIn[25:0], 2'b00}), .out(multiplexer_1_out),
    .sel(IsJumpInstr));
  Multiplexer #(.enable("false"), .width(32)) multiplexer_2 (
    .in0(multiplexer_1_out), .in1(adder_2_out), .out(multiplexer_2_out), .sel(and_1_out));
  and and_1 (and_1_out, IsBranch, IsZero);
  Register #(.width(32)) PC (.D(multiplexer_2_out), .clk(Clkin), .Q(InstrAddressOut));  // open: en, clr
  Multiplexer #(.enable("false"), .width(5)) multiplexer_3 (
    .in0(InstrIn[15:11]), .in1(InstrIn[20:16]), .out(multiplexer_3_out), .sel(IsIType));
  Multiplexer #(.enable("false"), .width(32)) multiplexer_4 (
    .in0(MemoryAddress), .in1(DataValueFromMemoryIn), .out(multiplexer_4_out), .sel(MemoryRead));
  assign SignExtendedImmediate = {{16{InstrIn[15]}}, InstrIn[15:0]};  // Bit_Extender bit_extender_1
  RegFile regfile_1 (
    .A(InstrIn[25:21]), .B(InstrIn[20:16]), .Dest(multiplexer_3_out), .Data(multiplexer_4_out),
    .Write(RegWrite), .AValue(AValue), .BValue(DataToWrite));  // open: Clkin
  Multiplexer #(.enable("false"), .width(32)) multiplexer_5 (
    .in0(DataToWrite), .in1(SignExtendedImmediate), .out(multiplexer_5_out), .sel(IsIType));
  ALU alu_1 (.OpSelect(AluControl), .A(AValue), .B(multiplexer_5_out), .Result(MemoryAddress), .IsZeroOut(IsZero));

  // Other names for the same wires on the sheet: AluResult[31:0] = MemoryAddress; BValue[31:0] = DataToWrite;
  //   Clk = Clkin; DataValueFromMemory[31:0] = DataValueFromMemoryIn; Instr[31:0] = InstrIn;
  //   InstrAddress[31:0] = InstrAddressOut; Immediate[15:0] = InstrIn[15:0]; JumpAddress[27:2] = InstrIn[25:0];
  //   JumpAddressFromInst[25:0] = InstrIn[25:0]; Rd[4:0] = InstrIn[15:11]; Rt[4:0] = InstrIn[20:16];
  //   Rs[4:0] = InstrIn[25:21]; PCPlus4[31:28] = JumpAddress; TopPCPlus4[3:0] = JumpAddress;
  //   MemoryWrite = WriteToMemoryOut
endmodule

module ALU (
  input  OpSelect,
  input  [31:0] A,
  input  [31:0] B,
  output [31:0] Result,
  output IsZeroOut
);
endmodule

module RegFile (
  input  [4:0] A,
  input  [4:0] B,
  input  [4:0] Dest,
  input  [31:0] Data,
  input  Write,
  input  Clkin,
  output [31:0] AValue,
  output [31:0] BValue
);

  wire demultiplexer_1_out0, demultiplexer_1_out1, demultiplexer_1_out2, demultiplexer_1_out3;
  wire [31:0] Reg0_q, Reg1_q, Reg2_q, Reg3_q;

  Demultiplexer #(.enable("false"), .select(5)) demultiplexer_1 (
    .out0(demultiplexer_1_out0), .out1(demultiplexer_1_out1), .out2(demultiplexer_1_out2),
    .out3(demultiplexer_1_out3), .in(Write), .sel(Dest));  // open: out4, out5, out6, out7, out8, out9, out10, out11, out12, out13, out14, out15, out16, out17, out18, out19, out20, out21, out22, out23, out24, out25, out26, out27, out28, out29, out30, out31
  Register #(.width(32)) Reg0 (.D(Data), .en(demultiplexer_1_out0), .clk(Clkin), .Q(Reg0_q));  // open: clr
  Register #(.width(32)) Reg1 (.D(Data), .en(demultiplexer_1_out1), .clk(Clkin), .Q(Reg1_q));  // open: clr
  Register #(.width(32)) Reg2 (.D(Data), .en(demultiplexer_1_out2), .clk(Clkin), .Q(Reg2_q));  // open: clr
  Register #(.width(32)) Reg3 (.D(Data), .en(demultiplexer_1_out3), .clk(Clkin), .Q(Reg3_q));  // open: clr
  Multiplexer #(.enable("false"), .select(5), .width(32)) multiplexer_1 (
    .in0(Reg0_q), .in1(Reg1_q), .in2(Reg2_q), .in3(Reg3_q), .out(AValue), .sel(A));  // open: in4, in5, in6, in7, in8, in9, in10, in11, in12, in13, in14, in15, in16, in17, in18, in19, in20, in21, in22, in23, in24, in25, in26, in27, in28, in29, in30, in31

  // Other names for the same wires on the sheet: Clk = Clkin; DataVal[31:0] = Data; DestPin[4:0] = Dest;
  //   WriteEnable = Write
endmodule

module InstDecoder (
  input  [5:0] OpCode,
  output RegWrite,
  output IsIType,
  output IsBranch,
  output IsJump,
  output MemWrite
);
endmodule
